// Logisim project 实验1-CS200X-0618-Yuigahama.circ as structural Verilog: 5 circuits, main circuit 一位二进制半加器
module \一位二进制半加器  (
  input  A,
  input  B,
  output S,
  output C
);

  xor xor_1 (S, A, B);
  and and_1 (C, A, B);
endmodule

module \一位二进制全加器  (
  input  C_prime,
  input  A,
  input  B,
  output S,
  output C
);

  wire and_1_out, and_2_out, and_3_out;

  xor xor_1 (S, C_prime, A, B);
  and and_1 (and_1_out, C_prime, A);
  and and_2 (and_2_out, C_prime, B);
  and and_3 (and_3_out, A, B);
  or or_1 (C, and_1_out, and_2_out, and_3_out);
endmodule

module \串行进位并行加法器  (
  input  C0,
  input  A0,
  input  A1,
  input  A2,
  input  A3,
  input  B0,
  input  B1,
  input  B2,
  input  B3,
  output S0,
  output S1,
  output S2,
  output S3,
  output C4
);

  wire \一位二进制全加器_1_c , \一位二进制全加器_2_c , \一位二进制全加器_3_c ;

  \一位二进制全加器  \u_一位二进制全加器_1  (.C_prime(C0), .A(A0), .B(B0), .S(S0), .C(\一位二进制全加器_1_c ));
  \一位二进制全加器  \u_一位二进制全加器_2  (.C_prime(\一位二进制全加器_1_c ), .A(A1), .B(B1), .S(S1), .C(\一位二进制全加器_2_c ));
  \一位二进制全加器  \u_一位二进制全加器_3  (.C_prime(\一位二进制全加器_2_c ), .A(A2), .B(B2), .S(S2), .C(\一位二进制全加器_3_c ));
  \一位二进制全加器  \u_一位二进制全加器_4  (.C_prime(\一位二进制全加器_3_c ), .A(A3), .B(B3), .S(S3), .C(C4));
endmodule

module \先行进位并行加法器  (
  input  A3,
  input  B3,
  input  A2,
  input  B2,
  input  A1,
  input  B1,
  input  A0,
  input  B0,
  input  C0,
  output C4,
  output S3,
  output S2,
  output S1,
  output S0
);

  wire and_1_out, and_2_out, and_3_out, and_4_out, and_5_out, and_6_out, and_7_out, and_8_out, and_9_out,
       and_10_out, and_11_out, and_12_out, and_13_out, and_14_out, or_2_out, or_3_out, or_4_out, or_5_out,
       or_6_out, or_7_out, or_8_out;

  and and_1 (and_1_out, and_14_out, or_5_out, or_3_out, or_2_out);
  and and_2 (and_2_out, or_8_out, or_5_out, or_3_out, or_2_out, C0);
  and and_3 (and_3_out, and_9_out, or_2_out);
  and and_4 (and_4_out, and_12_out, or_3_out, or_2_out);
  or or_1 (C4, and_2_out, and_1_out, and_4_out, and_3_out, and_7_out);
  or or_2 (or_2_out, B3, A3);
  and and_5 (and_5_out, or_8_out, or_5_out, or_3_out, C0);
  and and_6 (and_6_out, and_14_out, or_5_out, or_3_out);
  and and_7 (and_7_out, A3, B3);
  or or_3 (or_3_out, B2, A2);
  and and_8 (and_8_out, and_12_out, or_3_out);
  or or_4 (or_4_out, and_5_out, and_6_out, and_8_out, and_9_out);
  xor xor_1 (S3, or_4_out, and_7_out, or_2_out);
  and and_9 (and_9_out, A2, B2);
  or or_5 (or_5_out, B1, A1);
  and and_10 (and_10_out, and_14_out, or_5_out);
  and and_11 (and_11_out, or_8_out, or_5_out, C0);
  or or_6 (or_6_out, and_11_out, and_10_out, and_12_out);
  xor xor_2 (S2, or_6_out, and_9_out, or_3_out);
  and and_12 (and_12_out, A1, B1);
  and and_13 (and_13_out, or_8_out, C0);
  or or_7 (or_7_out, and_13_out, and_14_out);
  xor xor_3 (S1, or_7_out, and_12_out, or_5_out);
  or or_8 (or_8_out, B0, A0);
  and and_14 (and_14_out, A0, B0);
  xor xor_4 (S0, C0, or_8_out, and_14_out);
endmodule

module \先行进位并行加法器测试电路  (
  input  C0,
  input  A3,
  input  A2,
  input  A1,
  input  A0,
  input  B3,
  input  B2,
  input  B1,
  input  B0,
  output S3,
  output S2,
  output S1,
  output S0,
  output C4
);

  \先行进位并行加法器  \u_先行进位并行加法器_1  (
    .C4(C4), .C0(C0), .A3(A3), .B3(B3), .A2(B2), .B2(A2), .A1(A1), .B1(B1), .A0(A0), .B0(B0), .S3(S3),
    .S2(S2), .S1(S1), .S0(S0));
endmodule
