// Logisim project 实验3-CS2007-0618-Yuigahama.circ as structural Verilog: 6 circuits, main circuit 四位乘法器
module \四位乘法器  (
  input  [3:0] a_3_0,
  input  [3:0] b_3_0,
  output [7:0] p_7_0
);

  wire [7:0] adder_1_out, adder_2_out, adder_3_out, adder_4_out, bit_extender_1_out, multiplexer_1_out,
       multiplexer_2_out, multiplexer_3_out, shifter_1_out, shifter_2_out, shifter_3_out;

  assign bit_extender_1_out = {{4{1'b0}}, b_3_0};  // Bit_Extender bit_extender_1
  Adder #(.width(8)) adder_1 (.a({8{1'b0}}), .b(bit_extender_1_out), .out(adder_1_out));  // open: cin, cout
  Shifter #(.width(8), .shift("ll")) shifter_1 (.in(bit_extender_1_out), .\dist (3'b001), .out(shifter_1_out));
  Multiplexer #(.select(1), .width(8), .disabled("Z"), .enable("false")) multiplexer_1 (
    .in0({8{1'b0}}), .in1(adder_1_out), .out(multiplexer_1_out), .sel(a_3_0[0]));
  Adder #(.width(8)) adder_2 (.a(multiplexer_1_out), .b(shifter_1_out), .out(adder_2_out));  // open: cin, cout
  Multiplexer #(.select(1), .width(8), .disabled("Z"), .enable("false")) multiplexer_2 (
    .in0(multiplexer_1_out), .in1(adder_2_out), .out(multiplexer_2_out), .sel(a_3_0[1]));
  Shifter #(.width(8), .shift("ll")) shifter_2 (.in(shifter_1_out), .\dist (3'b001), .out(shifter_2_out));
  Adder #(.width(8)) adder_3 (.a(multiplexer_2_out), .b(shifter_2_out), .out(adder_3_out));  // open: cin, cout
  Shifter #(.width(8), .shift("ll")) shifter_3 (.in(shifter_2_out), .\dist (3'b001), .out(shifter_3_out));
  Multiplexer #(.select(1), .width(8), .disabled("Z"), .enable("false")) multiplexer_3 (
    .in0(multiplexer_2_out), .in1(adder_3_out), .out(multiplexer_3_out), .sel(a_3_0[2]));
  Adder #(.width(8)) adder_4 (.a(multiplexer_3_out), .b(shifter_3_out), .out(adder_4_out));  // open: cin, cout
  Multiplexer #(.select(1), .width(8), .disabled("Z"), .enable("false")) multiplexer_4 (
    .in0(multiplexer_3_out), .in1(adder_4_out), .out(p_7_0), .sel(a_3_0[3]));
endmodule

module \四位乘法器测试电路  (
  input  [3:0] a_3_0,
  input  [3:0] b_3_0,
  output [7:0] p_7_0
);

  \四位乘法器  \u_四位乘法器_1  (.a_3_0(a_3_0), .b_3_0(b_3_0), .p_7_0(p_7_0));
endmodule

module \_32X4乘法器  (
  input  [3:0] a_3_0,
  input  [31:0] b_31_0,
  output [31:0] p_63_32,
  output [31:0] p_31_0
);

  wire [31:0] adder_1_out, adder_2_out, adder_3_out, adder_4_out, adder_5_out, adder_6_out, adder_7_out,
       adder_8_out, multiplexer_1_out, multiplexer_2_out, multiplexer_3_out, multiplexer_4_out,
       multiplexer_5_out, multiplexer_6_out, multiplexer_7_out, shifter_1_out, shifter_2_out, shifter_3_out,
       shifter_4_out, shifter_5_out, shifter_6_out, shifter_7_out;

  Shifter #(.width(32), .shift("lr")) shifter_1 (.in(b_31_0), .\dist (5'b00001), .out(shifter_1_out));
  Adder #(.width(32)) adder_1 (.a({32{1'b0}}), .b(shifter_1_out), .out(adder_1_out));  // open: cin, cout
  Shifter #(.width(32), .shift("lr")) shifter_2 (.in(shifter_1_out), .\dist (5'b00001), .out(shifter_2_out));
  Adder #(.width(32)) adder_2 (.a({32{1'b0}}), .b(b_31_0), .out(adder_2_out));  // open: cin, cout
  Shifter #(.width(32), .shift("ll")) shifter_3 (.in(b_31_0), .\dist (5'b00001), .out(shifter_3_out));
  Multiplexer #(.select(1), .width(32), .disabled("Z"), .enable("false")) multiplexer_1 (
    .in0({32{1'b0}}), .in1(adder_1_out), .out(multiplexer_1_out), .sel(a_3_0[3]));
  Adder #(.width(32)) adder_3 (.a(multiplexer_1_out), .b(shifter_2_out), .out(adder_3_out));  // open: cin, cout
  Multiplexer #(.select(1), .width(32), .disabled("Z"), .enable("false")) multiplexer_2 (
    .in0({32{1'b0}}), .in1(adder_2_out), .out(multiplexer_2_out), .sel(a_3_0[0]));
  Adder #(.width(32)) adder_4 (.a(multiplexer_2_out), .b(shifter_3_out), .out(adder_4_out));  // open: cin, cout
  Multiplexer #(.select(1), .width(32), .disabled("Z"), .enable("false")) multiplexer_3 (
    .in0(multiplexer_1_out), .in1(adder_3_out), .out(multiplexer_3_out), .sel(a_3_0[2]));
  Shifter #(.width(32), .shift("lr")) shifter_4 (.in(shifter_2_out), .\dist (5'b00001), .out(shifter_4_out));
  Multiplexer #(.select(1), .width(32), .disabled("Z"), .enable("false")) multiplexer_4 (
    .in0(multiplexer_2_out), .in1(adder_4_out), .out(multiplexer_4_out), .sel(a_3_0[1]));
  Shifter #(.width(32), .shift("ll")) shifter_5 (.in(shifter_3_out), .\dist (5'b00001), .out(shifter_5_out));
  Adder #(.width(32)) adder_5 (.a(multiplexer_3_out), .b(shifter_4_out), .out(adder_5_out));  // open: cin, cout
  Shifter #(.width(32), .shift("lr")) shifter_6 (.in(shifter_4_out), .\dist (5'b00001), .out(shifter_6_out));
  Adder #(.width(32)) adder_6 (.a(multiplexer_4_out), .b(shifter_5_out), .out(adder_6_out));  // open: cin, cout
  Shifter #(.width(32), .shift("ll")) shifter_7 (.in(shifter_5_out), .\dist (5'b00001), .out(shifter_7_out));
  Multiplexer #(.select(1), .width(32), .disabled("Z"), .enable("false")) multiplexer_5 (
    .in0(multiplexer_3_out), .in1(adder_5_out), .out(multiplexer_5_out), .sel(a_3_0[1]));
  Adder #(.width(32)) adder_7 (.a(multiplexer_5_out), .b(shifter_6_out), .out(adder_7_out));  // open: cin, cout
  Multiplexer #(.select(1), .width(32), .disabled("Z"), .enable("false")) multiplexer_6 (
    .in0(multiplexer_4_out), .in1(adder_6_out), .out(multiplexer_6_out), .sel(a_3_0[2]));
  Adder #(.width(32)) adder_8 (.a(multiplexer_6_out), .b(shifter_7_out), .out(adder_8_out));  // open: cin, cout
  Multiplexer #(.select(1), .width(32), .disabled("Z"), .enable("false")) multiplexer_7 (
    .in0(multiplexer_5_out), .in1(adder_7_out), .out(multiplexer_7_out), .sel(a_3_0[0]));
  Multiplexer #(.select(1), .width(32), .disabled("Z"), .enable("false")) multiplexer_8 (
    .in0(multiplexer_6_out), .in1(adder_8_out), .out(p_31_0), .sel(a_3_0[3]));
  Shifter #(.width(32), .shift("lr")) shifter_8 (.in(multiplexer_7_out), .\dist (5'b11100), .out(p_63_32));
endmodule

module \_32X4乘法器测试电路  (
  input  [3:0] a_3_0,
  input  [31:0] b_31_0,
  output [31:0] p_63_32,
  output [31:0] p_31_0
);

  \_32X4乘法器  \u_32x4乘法器_1  (.a_3_0(a_3_0), .b_31_0(b_31_0), .p_63_32(p_63_32), .p_31_0(p_31_0));
endmodule

module \_32X32乘法器  (
  input  [31:0] a_31_0,
  input  [31:0] b_31_0,
  output [31:0] p_63_32,
  output [31:0] p_31_0
);

  wire [31:0] adder_1_out, adder_2_out, adder_3_out, adder_4_out, adder_5_out, adder_6_out, adder_7_out,
       adder_8_out, adder_9_out, adder_10_out, adder_11_out, adder_12_out, adder_13_out, adder_14_out,
       adder_15_out, adder_16_out, adder_17_out, adder_18_out, adder_19_out, \n32x4乘法器_1_p_31_0 ,
       \n32x4乘法器_1_p_63_32 , \n32x4乘法器_2_p_31_0 , \n32x4乘法器_2_p_63_32 , \n32x4乘法器_3_p_31_0 ,
       \n32x4乘法器_3_p_63_32 , \n32x4乘法器_4_p_31_0 , \n32x4乘法器_4_p_63_32 , \n32x4乘法器_5_p_31_0 ,
       \n32x4乘法器_5_p_63_32 , \n32x4乘法器_6_p_31_0 , \n32x4乘法器_6_p_63_32 , \n32x4乘法器_7_p_31_0 ,
       \n32x4乘法器_7_p_63_32 , \n32x4乘法器_8_p_31_0 , \n32x4乘法器_8_p_63_32 , shifter_1_out, shifter_2_out,
       shifter_3_out, shifter_4_out, shifter_5_out, shifter_6_out, shifter_7_out, shifter_8_out,
       shifter_9_out, shifter_10_out, shifter_11_out, shifter_12_out, shifter_13_out, shifter_14_out,
       shifter_15_out, shifter_16_out, shifter_17_out, shifter_18_out, shifter_19_out, shifter_20_out,
       shifter_21_out;

  \_32X4乘法器  \u_32x4乘法器_1  (
    .a_3_0(a_31_0[31:28]), .b_31_0(b_31_0), .p_63_32(\n32x4乘法器_1_p_63_32 ), .p_31_0(\n32x4乘法器_1_p_31_0 ));
  \_32X4乘法器  \u_32x4乘法器_2  (
    .a_3_0(a_31_0[27:24]), .b_31_0(b_31_0), .p_63_32(\n32x4乘法器_2_p_63_32 ), .p_31_0(\n32x4乘法器_2_p_31_0 ));
  \_32X4乘法器  \u_32x4乘法器_3  (
    .a_3_0(a_31_0[23:20]), .b_31_0(b_31_0), .p_63_32(\n32x4乘法器_3_p_63_32 ), .p_31_0(\n32x4乘法器_3_p_31_0 ));
  \_32X4乘法器  \u_32x4乘法器_4  (
    .a_3_0(a_31_0[19:16]), .b_31_0(b_31_0), .p_63_32(\n32x4乘法器_4_p_63_32 ), .p_31_0(\n32x4乘法器_4_p_31_0 ));
  \_32X4乘法器  \u_32x4乘法器_5  (
    .a_3_0(a_31_0[15:12]), .b_31_0(b_31_0), .p_63_32(\n32x4乘法器_5_p_63_32 ), .p_31_0(\n32x4乘法器_5_p_31_0 ));
  \_32X4乘法器  \u_32x4乘法器_6  (
    .a_3_0(a_31_0[11:8]), .b_31_0(b_31_0), .p_63_32(\n32x4乘法器_6_p_63_32 ), .p_31_0(\n32x4乘法器_6_p_31_0 ));
  \_32X4乘法器  \u_32x4乘法器_7  (
    .a_3_0(a_31_0[7:4]), .b_31_0(b_31_0), .p_63_32(\n32x4乘法器_7_p_63_32 ), .p_31_0(\n32x4乘法器_7_p_31_0 ));
  \_32X4乘法器  \u_32x4乘法器_8  (
    .a_3_0(a_31_0[3:0]), .b_31_0(b_31_0), .p_63_32(\n32x4乘法器_8_p_63_32 ), .p_31_0(\n32x4乘法器_8_p_31_0 ));
  Shifter #(.width(32), .shift("ll")) shifter_1 (.in(\n32x4乘法器_1_p_63_32 ), .\dist (5'b11100), .out(shifter_1_out));
  Shifter #(.width(32), .shift("lr")) shifter_2 (.in(\n32x4乘法器_1_p_31_0 ), .\dist (5'b00100), .out(shifter_2_out));
  Shifter #(.width(32), .shift("ll")) shifter_3 (.in(\n32x4乘法器_2_p_63_32 ), .\dist (5'b11000), .out(shifter_3_out));
  Shifter #(.width(32), .shift("lr")) shifter_4 (.in(\n32x4乘法器_2_p_31_0 ), .\dist (5'b01000), .out(shifter_4_out));
  Shifter #(.width(32), .shift("ll")) shifter_5 (.in(\n32x4乘法器_3_p_63_32 ), .\dist (5'b10100), .out(shifter_5_out));
  Shifter #(.width(32), .shift("lr")) shifter_6 (.in(\n32x4乘法器_3_p_31_0 ), .\dist (5'b01100), .out(shifter_6_out));
  Shifter #(.width(32), .shift("ll")) shifter_7 (.in(\n32x4乘法器_4_p_63_32 ), .\dist (5'b10000), .out(shifter_7_out));
  Shifter #(.width(32), .shift("lr")) shifter_8 (.in(\n32x4乘法器_4_p_31_0 ), .\dist (5'b10000), .out(shifter_8_out));
  Shifter #(.width(32), .shift("ll")) shifter_9 (.in(\n32x4乘法器_5_p_63_32 ), .\dist (5'b01100), .out(shifter_9_out));
  Shifter #(.width(32), .shift("lr")) shifter_10 (.in(\n32x4乘法器_5_p_31_0 ), .\dist (5'b10100), .out(shifter_10_out));
  Shifter #(.width(32), .shift("ll")) shifter_11 (.in(\n32x4乘法器_6_p_63_32 ), .\dist (5'b01000), .out(shifter_11_out));
  Shifter #(.width(32), .shift("lr")) shifter_12 (.in(\n32x4乘法器_6_p_31_0 ), .\dist (5'b11000), .out(shifter_12_out));
  Shifter #(.width(32), .shift("ll")) shifter_13 (.in(\n32x4乘法器_7_p_63_32 ), .\dist (5'b00100), .out(shifter_13_out));
  Shifter #(.width(32), .shift("lr")) shifter_14 (.in(\n32x4乘法器_7_p_31_0 ), .\dist (5'b11100), .out(shifter_14_out));
  Adder #(.width(32)) adder_1 (.a(shifter_1_out), .b(shifter_2_out), .out(adder_1_out));  // open: cin, cout
  Shifter #(.width(32), .shift("ll")) shifter_15 (.in(\n32x4乘法器_1_p_31_0 ), .\dist (5'b11100), .out(shifter_15_out));
  Adder #(.width(32)) adder_2 (.a(shifter_3_out), .b(shifter_4_out), .out(adder_2_out));  // open: cin, cout
  Shifter #(.width(32), .shift("ll")) shifter_16 (.in(\n32x4乘法器_2_p_31_0 ), .\dist (5'b11000), .out(shifter_16_out));
  Adder #(.width(32)) adder_3 (.a(shifter_5_out), .b(shifter_6_out), .out(adder_3_out));  // open: cin, cout
  Shifter #(.width(32), .shift("ll")) shifter_17 (.in(\n32x4乘法器_3_p_31_0 ), .\dist (5'b10100), .out(shifter_17_out));
  Adder #(.width(32)) adder_4 (.a(shifter_7_out), .b(shifter_8_out), .out(adder_4_out));  // open: cin, cout
  Shifter #(.width(32), .shift("ll")) shifter_18 (.in(\n32x4乘法器_4_p_31_0 ), .\dist (5'b10000), .out(shifter_18_out));
  Adder #(.width(32)) adder_5 (.a(shifter_9_out), .b(shifter_10_out), .out(adder_5_out));  // open: cin, cout
  Shifter #(.width(32), .shift("ll")) shifter_19 (.in(\n32x4乘法器_5_p_31_0 ), .\dist (5'b01100), .out(shifter_19_out));
  Adder #(.width(32)) adder_6 (.a(shifter_11_out), .b(shifter_12_out), .out(adder_6_out));  // open: cin, cout
  Shifter #(.width(32), .shift("ll")) shifter_20 (.in(\n32x4乘法器_6_p_31_0 ), .\dist (5'b01000), .out(shifter_20_out));
  Adder #(.width(32)) adder_7 (.a(shifter_13_out), .b(shifter_14_out), .out(adder_7_out));  // open: cin, cout
  Shifter #(.width(32), .shift("ll")) shifter_21 (.in(\n32x4乘法器_7_p_31_0 ), .\dist (5'b00100), .out(shifter_21_out));
  Adder #(.width(32)) adder_8 (.a(shifter_15_out), .b(shifter_16_out), .out(adder_8_out));  // open: cin, cout
  Adder #(.width(32)) adder_9 (.a(adder_1_out), .b(adder_2_out), .out(adder_9_out));  // open: cin, cout
  Adder #(.width(32)) adder_10 (.a(adder_8_out), .b(shifter_17_out), .out(adder_10_out));  // open: cin, cout
  Adder #(.width(32)) adder_11 (.a(adder_9_out), .b(adder_3_out), .out(adder_11_out));  // open: cin, cout
  Adder #(.width(32)) adder_12 (.a(adder_10_out), .b(shifter_18_out), .out(adder_12_out));  // open: cin, cout
  Adder #(.width(32)) adder_13 (.a(adder_12_out), .b(shifter_19_out), .out(adder_13_out));  // open: cin, cout
  Adder #(.width(32)) adder_14 (.a(adder_11_out), .b(adder_4_out), .out(adder_14_out));  // open: cin, cout
  Adder #(.width(32)) adder_15 (.a(adder_13_out), .b(shifter_20_out), .out(adder_15_out));  // open: cin, cout
  Adder #(.width(32)) adder_16 (.a(adder_14_out), .b(adder_5_out), .out(adder_16_out));  // open: cin, cout
  Adder #(.width(32)) adder_17 (.a(adder_16_out), .b(adder_6_out), .out(adder_17_out));  // open: cin, cout
  Adder #(.width(32)) adder_18 (.a(adder_15_out), .b(shifter_21_out), .out(adder_18_out));  // open: cin, cout
  Adder #(.width(32)) adder_19 (.a(adder_17_out), .b(adder_7_out), .out(adder_19_out));  // open: cin, cout
  Adder #(.width(32)) adder_20 (.a(adder_18_out), .b(\n32x4乘法器_8_p_31_0 ), .out(p_31_0));  // open: cin, cout
  Adder #(.width(32)) adder_21 (.a(adder_19_out), .b(\n32x4乘法器_8_p_63_32 ), .out(p_63_32));  // open: cin, cout
endmodule

module \_32X32乘法器测试电路  (
  input  [31:0] a_31_0,
  input  [31:0] b_31_0,
  output [31:0] p_63_32,
  output [31:0] p_31_0
);

  \_32X32乘法器  \u_32x32乘法器_1  (.a_31_0(a_31_0), .b_31_0(b_31_0), .p_63_32(p_63_32), .p_31_0(p_31_0));
endmodule
