// Logisim project 实验2-CS200X-0618-Yuigahama.circ as structural Verilog: 10 circuits, main circuit 四位二进制可逆计数器
module \四位二进制可逆计数器  (
  input  CPD,
  input  CPU,
  input  A,
  input  B,
  input  C,
  input  D,
  input  nLD,
  input  CLR,
  output QA,
  output QB,
  output QC,
  output QD
);

  wire and_1_out, and_2_out, and_3_out, and_4_out, and_5_out, and_6_out, and_7_out, and_8_out, and_9_out,
       and_10_out, and_11_out, and_12_out, and_13_out, and_14_out, d_ff_1_qn, d_ff_2_qn, d_ff_3_qn,
       d_ff_4_qn, not_1_out, not_2_out, not_3_out, not_4_out, not_5_out, or_1_out, or_2_out, or_3_out,
       or_4_out, or_5_out, or_6_out, or_7_out, or_8_out;

  and and_1 (and_1_out, d_ff_1_qn, CPD);
  and and_2 (and_2_out, QA, CPU);
  and and_3 (and_3_out, d_ff_1_qn, d_ff_2_qn, CPD);
  and and_4 (and_4_out, QA, QB, CPU);
  and and_5 (and_5_out, d_ff_1_qn, d_ff_2_qn, d_ff_3_qn, CPD);
  and and_6 (and_6_out, QA, QB, QC, CPU);
  or or_1 (or_1_out, CPD, CPU);
  or or_2 (or_2_out, and_1_out, and_2_out);
  or or_3 (or_3_out, and_3_out, and_4_out);
  or or_4 (or_4_out, and_5_out, and_6_out);
  D_Flip_Flop #(.trigger("falling"), .Pre_Clr_Positions("LEGACY"), .NegatePresetClear("false"), .enable("true"), .NewFFLayout("false")) d_ff_1 (
    .clk(or_1_out), .D(d_ff_1_qn), .Q(QA), .Qn(d_ff_1_qn), .preset(and_7_out), .en(nLD), .reset(or_5_out));
  D_Flip_Flop #(.trigger("falling"), .Pre_Clr_Positions("LEGACY"), .NegatePresetClear("false"), .enable("true"), .NewFFLayout("false")) d_ff_2 (
    .clk(or_2_out), .D(d_ff_2_qn), .Q(QB), .Qn(d_ff_2_qn), .preset(and_9_out), .en(nLD), .reset(or_6_out));
  D_Flip_Flop #(.trigger("falling"), .Pre_Clr_Positions("LEGACY"), .NegatePresetClear("false"), .enable("true"), .NewFFLayout("false")) d_ff_3 (
    .clk(or_3_out), .D(d_ff_3_qn), .Q(QC), .Qn(d_ff_3_qn), .preset(and_11_out), .en(nLD), .reset(or_7_out));
  D_Flip_Flop #(.trigger("falling"), .Pre_Clr_Positions("LEGACY"), .NegatePresetClear("false"), .enable("true"), .NewFFLayout("false")) d_ff_4 (
    .clk(or_4_out), .D(d_ff_4_qn), .Q(QD), .Qn(d_ff_4_qn), .preset(and_13_out), .en(nLD), .reset(or_8_out));
  or or_5 (or_5_out, CLR, and_8_out);
  or or_6 (or_6_out, CLR, and_10_out);
  or or_7 (or_7_out, CLR, and_12_out);
  or or_8 (or_8_out, CLR, and_14_out);
  and and_7 (and_7_out, not_1_out, A);
  and and_8 (and_8_out, not_1_out, not_2_out);
  and and_9 (and_9_out, not_1_out, B);
  and and_10 (and_10_out, not_1_out, not_3_out);
  and and_11 (and_11_out, not_1_out, C);
  and and_12 (and_12_out, not_1_out, not_4_out);
  and and_13 (and_13_out, not_1_out, D);
  and and_14 (and_14_out, not_1_out, not_5_out);
  not not_1 (not_1_out, nLD);
  not not_2 (not_2_out, A);
  not not_3 (not_3_out, B);
  not not_4 (not_4_out, C);
  not not_5 (not_5_out, D);
endmodule

module \四位二进制可逆计数器测试电路  (
  input  CPU,
  input  CLR,
  input  CPD,
  input  D,
  input  C,
  input  B,
  input  A,
  input  nLD,
  output QD,
  output QC,
  output QB,
  output QA
);

  \四位二进制可逆计数器  \u_四位二进制可逆计数器_1  (
    .CPD(CPD), .CPU(CPU), .QA(QA), .A(A), .QB(QB), .B(B), .QC(QC), .C(C), .QD(QD), .D(D), .nLD(nLD), .CLR(CLR));
endmodule

module \二进制转8421码电路  (
  input  A3,
  input  A2,
  input  A1,
  input  A0,
  output S7,
  output S6,
  output S5,
  output S4,
  output S3,
  output S2,
  output S1,
  output S0
);

  wire or_1_out;

  or or_1 (or_1_out, A1, A2);
  and and_1 (S4, or_1_out, A3);
  \四位二进制并行加法器  \u_四位二进制并行加法器_1  (
    .C0(1'b0), .A3(A3), .B3(1'b0), .A2(A2), .B2(S4), .A1(A1), .B1(S4), .A0(A0), .B0(1'b0), .S3(S3), .S2(S2),
    .S1(S1), .S0(S0));  // open: C4

  assign S5 = 1'b0;
  assign S6 = 1'b0;
  assign S7 = 1'b0;
endmodule

module \二进制转8421码测试电路  (
  input  A3,
  input  A2,
  input  A1,
  input  A0,
  output S7,
  output S6,
  output S5,
  output S4,
  output S3,
  output S2,
  output S0,
  output S0_2
);

  \二进制转8421码电路  \u_二进制转8421码电路_1  (
    .S7(S7), .S6(S6), .S5(S5), .S4(S4), .S3(S3), .S2(S2), .S1(S0), .S0(S0_2), .A3(A3), .A2(A2), .A1(A1),
    .A0(A0));
endmodule

module \显示电路  (
  input  A3,
  input  A2,
  input  A1,
  input  A0,
  output a,
  output b,
  output c,
  output d,
  output e,
  output f,
  output g
);

  wire and_1_out, and_2_out, and_3_out, and_4_out, and_5_out, and_6_out, and_7_out, and_8_out, and_9_out,
       and_10_out, and_11_out, and_12_out, and_13_out, and_14_out, and_15_out, and_16_out, and_17_out,
       and_18_out, and_19_out, and_20_out, and_21_out, and_22_out, and_23_out, and_24_out, and_25_out,
       and_26_out, not_1_out, not_2_out, not_3_out, not_4_out, not_5_out, not_6_out, not_7_out, not_8_out,
       not_9_out, not_10_out, not_11_out, not_12_out, not_13_out, not_14_out, not_15_out, not_16_out,
       not_17_out, not_18_out, not_19_out, not_20_out, not_21_out, not_22_out, not_23_out, not_24_out,
       not_25_out, not_26_out, not_27_out, not_28_out, not_29_out, not_30_out, not_31_out, not_32_out,
       not_33_out, not_34_out, not_35_out, not_36_out, not_37_out, not_38_out, not_39_out, not_40_out,
       not_41_out, not_42_out, not_43_out, not_44_out, not_45_out, not_46_out, not_47_out, not_48_out,
       not_49_out, not_50_out, not_51_out, not_52_out, not_53_out;

  not not_1 (not_1_out, A3);
  and and_1 (and_1_out, not_1_out, A1);
  not not_2 (not_2_out, A2);
  not not_3 (not_3_out, A1);
  and and_2 (and_2_out, not_2_out, not_3_out, not_4_out);
  not not_4 (not_4_out, A0);
  and and_3 (and_3_out, A3, not_5_out, not_6_out);
  not not_5 (not_5_out, A2);
  not not_6 (not_6_out, A1);
  not not_7 (not_7_out, A3);
  and and_4 (and_4_out, not_7_out, A2, not_8_out, A0);
  not not_8 (not_8_out, A1);
  not not_9 (not_9_out, A3);
  and and_5 (and_5_out, not_9_out, not_10_out);
  not not_10 (not_10_out, A2);
  not not_11 (not_11_out, A3);
  and and_6 (and_6_out, not_11_out, not_12_out, not_13_out);
  not not_12 (not_12_out, A1);
  not not_13 (not_13_out, A0);
  not not_14 (not_14_out, A2);
  and and_7 (and_7_out, not_14_out, not_15_out);
  not not_15 (not_15_out, A1);
  not not_16 (not_16_out, A3);
  and and_8 (and_8_out, not_16_out, A1, A0);
  not not_17 (not_17_out, A2);
  and and_9 (and_9_out, not_17_out, not_18_out);
  not not_18 (not_18_out, A1);
  not not_19 (not_19_out, A3);
  and and_10 (and_10_out, not_19_out, A0);
  not not_20 (not_20_out, A3);
  and and_11 (and_11_out, not_20_out, A2);
  not not_21 (not_21_out, A2);
  and and_12 (and_12_out, not_21_out, not_22_out, not_23_out);
  not not_22 (not_22_out, A1);
  not not_23 (not_23_out, A0);
  not not_24 (not_24_out, A3);
  not not_25 (not_25_out, A2);
  and and_13 (and_13_out, not_24_out, not_25_out, A1);
  and and_14 (and_14_out, A3, not_26_out, not_27_out);
  not not_26 (not_26_out, A2);
  not not_27 (not_27_out, A1);
  not not_28 (not_28_out, A3);
  and and_15 (and_15_out, not_28_out, A1, not_29_out);
  not not_29 (not_29_out, A0);
  not not_30 (not_30_out, A3);
  and and_16 (and_16_out, not_30_out, A2, not_31_out, A0);
  not not_31 (not_31_out, A1);
  not not_32 (not_32_out, A2);
  not not_33 (not_33_out, A1);
  and and_17 (and_17_out, not_32_out, not_33_out, not_34_out);
  not not_34 (not_34_out, A0);
  not not_35 (not_35_out, A3);
  and and_18 (and_18_out, not_35_out, A1, not_36_out);
  not not_36 (not_36_out, A0);
  not not_37 (not_37_out, A3);
  not not_38 (not_38_out, A1);
  and and_19 (and_19_out, not_37_out, not_38_out, not_39_out);
  not not_39 (not_39_out, A0);
  not not_40 (not_40_out, A3);
  and and_20 (and_20_out, not_40_out, A2, not_41_out);
  not not_41 (not_41_out, A1);
  not not_42 (not_42_out, A3);
  and and_21 (and_21_out, not_42_out, A2, not_43_out);
  not not_43 (not_43_out, A0);
  and and_22 (and_22_out, A3, not_44_out, not_45_out);
  not not_44 (not_44_out, A2);
  not not_45 (not_45_out, A1);
  not not_46 (not_46_out, A3);
  not not_47 (not_47_out, A2);
  and and_23 (and_23_out, not_46_out, not_47_out, A1);
  not not_48 (not_48_out, A3);
  and and_24 (and_24_out, not_48_out, A2, not_49_out);
  not not_49 (not_49_out, A1);
  not not_50 (not_50_out, A3);
  and and_25 (and_25_out, not_50_out, A2, not_51_out);
  not not_51 (not_51_out, A0);
  not not_52 (not_52_out, A2);
  and and_26 (and_26_out, A3, not_52_out, not_53_out);
  not not_53 (not_53_out, A1);
  or or_1 (a, and_1_out, and_2_out, and_3_out, and_4_out);
  or or_2 (b, and_5_out, and_6_out, and_7_out, and_8_out);
  or or_3 (c, and_9_out, and_10_out, and_11_out);
  or or_4 (d, and_12_out, and_13_out, and_14_out, and_15_out, and_16_out);
  or or_5 (e, and_17_out, and_18_out);
  or or_6 (f, and_19_out, and_20_out, and_21_out, and_22_out);
  or or_7 (g, and_23_out, and_24_out, and_25_out, and_26_out);
endmodule

module \显示电路测试电路  (
  input  A3,
  input  A2,
  input  A1,
  input  A0
);

  wire \二进制转8421码电路_1_s0 , \二进制转8421码电路_1_s1 , \二进制转8421码电路_1_s2 , \二进制转8421码电路_1_s3 , \二进制转8421码电路_1_s4 ,
       \二进制转8421码电路_1_s5 , \二进制转8421码电路_1_s6 , \二进制转8421码电路_1_s7 , \显示电路_1_a , \显示电路_1_b , \显示电路_1_c ,
       \显示电路_1_d , \显示电路_1_e , \显示电路_1_f , \显示电路_1_g , \显示电路_2_a , \显示电路_2_b , \显示电路_2_c , \显示电路_2_d ,
       \显示电路_2_e , \显示电路_2_f , \显示电路_2_g ;

  \显示电路  \u_显示电路_1  (
    .A3(\二进制转8421码电路_1_s7 ), .A2(\二进制转8421码电路_1_s6 ), .A1(\二进制转8421码电路_1_s5 ), .A0(\二进制转8421码电路_1_s4 ),
    .a(\显示电路_1_a ), .b(\显示电路_1_b ), .c(\显示电路_1_c ), .d(\显示电路_1_d ), .e(\显示电路_1_e ), .f(\显示电路_1_f ),
    .g(\显示电路_1_g ));
  _7_Segment_Display #(.active("true")) u_7_segment_display_1 (
    .g(\显示电路_1_g ), .f(\显示电路_1_f ), .a(\显示电路_1_a ), .b(\显示电路_1_b ), .e(\显示电路_1_e ), .d(\显示电路_1_d ),
    .c(\显示电路_1_c ));  // open: dp
  \二进制转8421码电路  \u_二进制转8421码电路_1  (
    .S7(\二进制转8421码电路_1_s7 ), .S6(\二进制转8421码电路_1_s6 ), .S5(\二进制转8421码电路_1_s5 ), .S4(\二进制转8421码电路_1_s4 ),
    .S3(\二进制转8421码电路_1_s3 ), .S2(\二进制转8421码电路_1_s2 ), .S1(\二进制转8421码电路_1_s1 ), .S0(\二进制转8421码电路_1_s0 ),
    .A3(A3), .A2(A2), .A1(A1), .A0(A0));
  _7_Segment_Display #(.active("true")) u_7_segment_display_2 (
    .g(\显示电路_2_g ), .f(\显示电路_2_f ), .a(\显示电路_2_a ), .b(\显示电路_2_b ), .e(\显示电路_2_e ), .d(\显示电路_2_d ),
    .c(\显示电路_2_c ));  // open: dp
  \显示电路  \u_显示电路_2  (
    .A3(\二进制转8421码电路_1_s3 ), .A2(\二进制转8421码电路_1_s2 ), .A1(\二进制转8421码电路_1_s1 ), .A0(\二进制转8421码电路_1_s0 ),
    .a(\显示电路_2_a ), .b(\显示电路_2_b ), .c(\显示电路_2_c ), .d(\显示电路_2_d ), .e(\显示电路_2_e ), .f(\显示电路_2_f ),
    .g(\显示电路_2_g ));
endmodule

module \报警电路  (
  input  CLR,
  input  D,
  input  C,
  input  B,
  input  A,
  input  nLD
);

  wire and_1_out, and_2_out, and_3_out, and_4_out, CPD_out, CPU_out, not_1_out, or_1_out, \四位二进制可逆计数器_1_qa ,
       \四位二进制可逆计数器_1_qb , \四位二进制可逆计数器_1_qc , \四位二进制可逆计数器_1_qd ;

  Button CPU (.out(CPU_out));
  Button CPD (.out(CPD_out));
  or or_1 (or_1_out, \四位二进制可逆计数器_1_qd , \四位二进制可逆计数器_1_qc , \四位二进制可逆计数器_1_qb , \四位二进制可逆计数器_1_qa );
  not not_1 (not_1_out, and_4_out);
  and and_1 (and_1_out, CPU_out, not_1_out);
  and and_2 (and_2_out, or_1_out, CPD_out);
  \四位二进制可逆计数器  \u_四位二进制可逆计数器_1  (
    .CPD(and_2_out), .CPU(and_1_out), .QA(\四位二进制可逆计数器_1_qa ), .A(A), .QB(\四位二进制可逆计数器_1_qb ), .B(B),
    .QC(\四位二进制可逆计数器_1_qc ), .C(C), .QD(\四位二进制可逆计数器_1_qd ), .D(D), .nLD(nLD), .CLR(CLR));
  LED #(.active("true")) ALERT (.in(and_3_out));
  and and_3 (and_3_out, CPU_out, and_4_out);
  and and_4 (and_4_out, \四位二进制可逆计数器_1_qd , \四位二进制可逆计数器_1_qc , \四位二进制可逆计数器_1_qb , \四位二进制可逆计数器_1_qa );
endmodule

module \小型实验室门禁系统  (
  input  CPU,
  input  CLR,
  input  CPD,
  output out_4,
  output out_5,
  output out_6,
  output out_7,
  output out_8,
  output out_9,
  output out_10,
  output out_11,
  output out_12,
  output out_13,
  output out_14,
  output out_15,
  output out_16,
  output out_17,
  output ALERT
);

  wire and_1_out, and_2_out, and_4_out, not_1_out, or_1_out, \二进制转8421码电路_1_s0 , \二进制转8421码电路_1_s1 ,
       \二进制转8421码电路_1_s2 , \二进制转8421码电路_1_s3 , \二进制转8421码电路_1_s4 , \二进制转8421码电路_1_s5 , \二进制转8421码电路_1_s6 ,
       \二进制转8421码电路_1_s7 , \四位二进制可逆计数器_1_qa , \四位二进制可逆计数器_1_qb , \四位二进制可逆计数器_1_qc , \四位二进制可逆计数器_1_qd ;

  \显示电路  \u_显示电路_1  (
    .A3(\二进制转8421码电路_1_s7 ), .A2(\二进制转8421码电路_1_s6 ), .A1(\二进制转8421码电路_1_s5 ), .A0(\二进制转8421码电路_1_s4 ),
    .a(out_4), .b(out_5), .c(out_6), .d(out_7), .e(out_8), .f(out_9), .g(out_10));
  \二进制转8421码电路  \u_二进制转8421码电路_1  (
    .S7(\二进制转8421码电路_1_s7 ), .S6(\二进制转8421码电路_1_s6 ), .S5(\二进制转8421码电路_1_s5 ), .S4(\二进制转8421码电路_1_s4 ),
    .S3(\二进制转8421码电路_1_s3 ), .S2(\二进制转8421码电路_1_s2 ), .S1(\二进制转8421码电路_1_s1 ), .S0(\二进制转8421码电路_1_s0 ),
    .A3(\四位二进制可逆计数器_1_qd ), .A2(\四位二进制可逆计数器_1_qc ), .A1(\四位二进制可逆计数器_1_qb ), .A0(\四位二进制可逆计数器_1_qa ));
  \显示电路  \u_显示电路_2  (
    .A3(\二进制转8421码电路_1_s3 ), .A2(\二进制转8421码电路_1_s2 ), .A1(\二进制转8421码电路_1_s1 ), .A0(\二进制转8421码电路_1_s0 ),
    .a(out_11), .b(out_12), .c(out_13), .d(out_14), .e(out_15), .f(out_16), .g(out_17));
  not not_1 (not_1_out, and_4_out);
  or or_1 (or_1_out, \四位二进制可逆计数器_1_qd , \四位二进制可逆计数器_1_qc , \四位二进制可逆计数器_1_qb , \四位二进制可逆计数器_1_qa );
  and and_1 (and_1_out, CPU, not_1_out);
  and and_2 (and_2_out, or_1_out, CPD);
  and and_3 (ALERT, CPU, and_4_out);
  \四位二进制可逆计数器  \u_四位二进制可逆计数器_1  (
    .CPD(and_2_out), .CPU(and_1_out), .QA(\四位二进制可逆计数器_1_qa ), .A(1'b0), .QB(\四位二进制可逆计数器_1_qb ), .B(1'b0),
    .QC(\四位二进制可逆计数器_1_qc ), .C(1'b0), .QD(\四位二进制可逆计数器_1_qd ), .D(1'b0), .nLD(1'b1), .CLR(CLR));
  and and_4 (and_4_out, \四位二进制可逆计数器_1_qd , \四位二进制可逆计数器_1_qc , \四位二进制可逆计数器_1_qb , \四位二进制可逆计数器_1_qa );
endmodule

module \小型门禁系统测试电路  (
);

  wire CLR_out, CPD_out, CPU_out, \小型实验室门禁系统_1_alert , \小型实验室门禁系统_1_out_4 , \小型实验室门禁系统_1_out_5 ,
       \小型实验室门禁系统_1_out_6 , \小型实验室门禁系统_1_out_7 , \小型实验室门禁系统_1_out_8 , \小型实验室门禁系统_1_out_9 ,
       \小型实验室门禁系统_1_out_10 , \小型实验室门禁系统_1_out_11 , \小型实验室门禁系统_1_out_12 , \小型实验室门禁系统_1_out_13 ,
       \小型实验室门禁系统_1_out_14 , \小型实验室门禁系统_1_out_15 , \小型实验室门禁系统_1_out_16 , \小型实验室门禁系统_1_out_17 ;

  Button CLR (.out(CLR_out));
  Button CPU (.out(CPU_out));
  Button CPD (.out(CPD_out));
  _7_Segment_Display #(.active("true")) u_7_segment_display_1 (
    .g(\小型实验室门禁系统_1_out_10 ), .f(\小型实验室门禁系统_1_out_9 ), .a(\小型实验室门禁系统_1_out_4 ), .b(\小型实验室门禁系统_1_out_5 ),
    .e(\小型实验室门禁系统_1_out_8 ), .d(\小型实验室门禁系统_1_out_7 ), .c(\小型实验室门禁系统_1_out_6 ));  // open: dp
  \小型实验室门禁系统  \u_小型实验室门禁系统_1  (
    .CLR(CLR_out), .out_4(\小型实验室门禁系统_1_out_4 ), .out_5(\小型实验室门禁系统_1_out_5 ), .out_6(\小型实验室门禁系统_1_out_6 ),
    .out_7(\小型实验室门禁系统_1_out_7 ), .out_8(\小型实验室门禁系统_1_out_8 ), .out_9(\小型实验室门禁系统_1_out_9 ),
    .out_10(\小型实验室门禁系统_1_out_10 ), .out_11(\小型实验室门禁系统_1_out_11 ), .out_12(\小型实验室门禁系统_1_out_12 ),
    .out_13(\小型实验室门禁系统_1_out_13 ), .out_14(\小型实验室门禁系统_1_out_14 ), .out_15(\小型实验室门禁系统_1_out_15 ),
    .out_16(\小型实验室门禁系统_1_out_16 ), .out_17(\小型实验室门禁系统_1_out_17 ), .ALERT(\小型实验室门禁系统_1_alert ), .CPU(CPU_out),
    .CPD(CPD_out));
  _7_Segment_Display #(.active("true")) u_7_segment_display_2 (
    .g(\小型实验室门禁系统_1_out_17 ), .f(\小型实验室门禁系统_1_out_16 ), .a(\小型实验室门禁系统_1_out_11 ), .b(\小型实验室门禁系统_1_out_12 ),
    .e(\小型实验室门禁系统_1_out_15 ), .d(\小型实验室门禁系统_1_out_14 ), .c(\小型实验室门禁系统_1_out_13 ));  // open: dp
  LED #(.active("true")) ALERT (.in(\小型实验室门禁系统_1_alert ));
endmodule

module \四位二进制并行加法器  (
  input  A3,
  input  B3,
  input  A2,
  input  B2,
  input  A1,
  input  B1,
  input  A0,
  input  B0,
  input  C0,
  output C4,
  output S3,
  output S2,
  output S1,
  output S0
);

  wire and_1_out, and_2_out, and_3_out, and_4_out, and_5_out, and_6_out, and_7_out, and_8_out, and_9_out,
       and_10_out, and_11_out, and_12_out, and_13_out, and_14_out, or_2_out, or_3_out, or_4_out, or_5_out,
       or_6_out, or_7_out, or_8_out;

  and and_1 (and_1_out, and_14_out, or_5_out, or_3_out, or_2_out);
  and and_2 (and_2_out, or_8_out, or_5_out, or_3_out, or_2_out, C0);
  and and_3 (and_3_out, and_12_out, or_3_out, or_2_out);
  and and_4 (and_4_out, and_9_out, or_2_out);
  or or_1 (C4, and_2_out, and_1_out, and_3_out, and_4_out, and_7_out);
  or or_2 (or_2_out, B3, A3);
  and and_5 (and_5_out, and_14_out, or_5_out, or_3_out);
  and and_6 (and_6_out, or_8_out, or_5_out, or_3_out, C0);
  or or_3 (or_3_out, B2, A2);
  and and_7 (and_7_out, A3, B3);
  and and_8 (and_8_out, and_12_out, or_3_out);
  or or_4 (or_4_out, and_6_out, and_5_out, and_8_out, and_9_out);
  xor xor_1 (S3, or_4_out, and_7_out, or_2_out);
  or or_5 (or_5_out, B1, A1);
  and and_9 (and_9_out, A2, B2);
  and and_10 (and_10_out, or_8_out, or_5_out, C0);
  and and_11 (and_11_out, and_14_out, or_5_out);
  or or_6 (or_6_out, and_10_out, and_11_out, and_12_out);
  xor xor_2 (S2, or_6_out, and_9_out, or_3_out);
  and and_12 (and_12_out, A1, B1);
  and and_13 (and_13_out, or_8_out, C0);
  or or_7 (or_7_out, and_13_out, and_14_out);
  xor xor_3 (S1, or_7_out, and_12_out, or_5_out);
  and and_14 (and_14_out, A0, B0);
  or or_8 (or_8_out, B0, A0);
  xor xor_4 (S0, C0, or_8_out, and_14_out);

  // Notes on the sheet:
  //   P3
  //   G3
  //   P2
  //   G2
  //   P1
  //   P0
  //   G1
  //   G0
endmodule
