// Logisim project 实验5-CS200X-0618-Yuigahama.circ as structural Verilog: 14 circuits, main circuit 四位二进制可逆计数器
module \四位二进制可逆计数器  (
  input  CPD,
  input  CPU,
  input  A,
  input  B,
  input  C,
  input  D,
  input  nLD,
  input  CLR,
  output QA,
  output QB,
  output QC,
  output QD
);

  wire and_1_out, and_2_out, and_3_out, and_4_out, and_5_out, and_6_out, and_7_out, and_8_out, and_9_out,
       and_10_out, and_11_out, and_12_out, and_13_out, and_14_out, d_ff_1_qn, d_ff_2_qn, d_ff_3_qn,
       d_ff_4_qn, not_1_out, not_2_out, not_3_out, not_4_out, not_5_out, or_1_out, or_2_out, or_3_out,
       or_4_out, or_5_out, or_6_out, or_7_out, or_8_out;

  and and_1 (and_1_out, d_ff_1_qn, CPD);
  and and_2 (and_2_out, QA, CPU);
  and and_3 (and_3_out, d_ff_1_qn, d_ff_2_qn, CPD);
  and and_4 (and_4_out, QA, QB, CPU);
  and and_5 (and_5_out, d_ff_1_qn, d_ff_2_qn, d_ff_3_qn, CPD);
  and and_6 (and_6_out, QA, QB, QC, CPU);
  or or_1 (or_1_out, CPD, CPU);
  or or_2 (or_2_out, and_1_out, and_2_out);
  or or_3 (or_3_out, and_3_out, and_4_out);
  or or_4 (or_4_out, and_5_out, and_6_out);
  D_Flip_Flop #(.trigger("falling"), .Pre_Clr_Positions("LEGACY"), .NegatePresetClear("false"), .enable("true"), .NewFFLayout("false")) d_ff_1 (
    .clk(or_1_out), .D(d_ff_1_qn), .Q(QA), .Qn(d_ff_1_qn), .preset(and_7_out), .en(nLD), .reset(or_5_out));
  D_Flip_Flop #(.trigger("falling"), .Pre_Clr_Positions("LEGACY"), .NegatePresetClear("false"), .enable("true"), .NewFFLayout("false")) d_ff_2 (
    .clk(or_2_out), .D(d_ff_2_qn), .Q(QB), .Qn(d_ff_2_qn), .preset(and_9_out), .en(nLD), .reset(or_6_out));
  D_Flip_Flop #(.trigger("falling"), .Pre_Clr_Positions("LEGACY"), .NegatePresetClear("false"), .enable("true"), .NewFFLayout("false")) d_ff_3 (
    .clk(or_3_out), .D(d_ff_3_qn), .Q(QC), .Qn(d_ff_3_qn), .preset(and_11_out), .en(nLD), .reset(or_7_out));
  D_Flip_Flop #(.trigger("falling"), .Pre_Clr_Positions("LEGACY"), .NegatePresetClear("false"), .enable("true"), .NewFFLayout("false")) d_ff_4 (
    .clk(or_4_out), .D(d_ff_4_qn), .Q(QD), .Qn(d_ff_4_qn), .preset(and_13_out), .en(nLD), .reset(or_8_out));
  or or_5 (or_5_out, CLR, and_8_out);
  or or_6 (or_6_out, CLR, and_10_out);
  or or_7 (or_7_out, CLR, and_12_out);
  or or_8 (or_8_out, CLR, and_14_out);
  and and_7 (and_7_out, not_1_out, A);
  and and_8 (and_8_out, not_1_out, not_2_out);
  and and_9 (and_9_out, not_1_out, B);
  and and_10 (and_10_out, not_1_out, not_3_out);
  and and_11 (and_11_out, not_1_out, C);
  and and_12 (and_12_out, not_1_out, not_4_out);
  and and_13 (and_13_out, not_1_out, D);
  and and_14 (and_14_out, not_1_out, not_5_out);
  not not_1 (not_1_out, nLD);
  not not_2 (not_2_out, A);
  not not_3 (not_3_out, B);
  not not_4 (not_4_out, C);
  not not_5 (not_5_out, D);
endmodule

module \六十进制计数器  (
  input  CPU,
  input  CPD,
  input  Adj,
  input  Clr,
  output Q0d,
  output Q1d,
  output Q0c,
  output Q1c,
  output Q0b,
  output nQcc,
  output Q1b,
  output Q0a,
  output Q1a
);

  wire and_1_out, and_2_out, and_3_out, and_4_out, and_6_out, not_1_out, not_2_out, not_3_out, not_4_out,
       or_1_out, or_2_out, or_3_out, or_4_out;

  and and_1 (and_1_out, CPD, Adj);
  or or_1 (or_1_out, Q0a, Q0b, or_3_out, Q0c, Q0d);
  and and_2 (and_2_out, or_1_out, and_1_out);
  or or_2 (or_2_out, and_4_out, Clr);
  not not_1 (not_1_out, Q0a);
  not not_2 (not_2_out, Q0c);
  \四位二进制可逆计数器  \u_四位二进制可逆计数器_1  (
    .CPD(and_2_out), .CPU(CPU), .QA(Q0a), .A(1'b1), .QB(Q0b), .B(1'b0), .QC(Q0c), .C(1'b0), .QD(Q0d),
    .D(1'b1), .nLD(not_3_out), .CLR(or_2_out));
  and and_3 (and_3_out, Q0a, Q0b, Q0c, Q0d);
  and and_4 (and_4_out, not_1_out, Q0b, not_2_out, Q0d);
  not not_3 (not_3_out, and_3_out);
  and and_5 (nQcc, not_4_out, and_6_out);
  not not_4 (not_4_out, Adj);
  or or_3 (or_3_out, Q1a, Q1b, Q1c, Q1d);
  and and_6 (and_6_out, Q1b, Q1c);
  or or_4 (or_4_out, and_6_out, Clr);
  \四位二进制可逆计数器  \u_四位二进制可逆计数器_2  (
    .CPD(and_3_out), .CPU(and_4_out), .QA(Q1a), .A(1'b0), .QB(Q1b), .B(1'b0), .QC(Q1c), .C(1'b0), .QD(Q1d),
    .D(1'b0), .nLD(1'b1), .CLR(or_4_out));
endmodule

module \六十进制计数器测试电路  (
  input  in_1,
  input  in_2,
  input  in_3,
  input  in_4
);

  wire button_1_out, button_2_out, button_3_out, \六十进制计数器_1_nqcc ;
  wire [3:0] \六十进制计数器_1_q0a , \六十进制计数器_1_q1a , \六十进制计数器_2_q0a , \六十进制计数器_2_q1a ;

  Button button_1 (.out(button_1_out));
  Button button_2 (.out(button_2_out));
  \六十进制计数器  \u_六十进制计数器_1  (
    .Adj(in_1), .Q0d(\六十进制计数器_1_q0a [3]), .Q0c(\六十进制计数器_1_q0a [2]), .Q0b(\六十进制计数器_1_q0a [1]),
    .Q0a(\六十进制计数器_1_q0a [0]), .nQcc(\六十进制计数器_1_nqcc ), .Q1d(\六十进制计数器_1_q1a [3]), .Q1c(\六十进制计数器_1_q1a [2]),
    .Q1b(\六十进制计数器_1_q1a [1]), .Q1a(\六十进制计数器_1_q1a [0]), .Clr(in_3), .CPU(button_1_out), .CPD(button_2_out));
  Hex_Digit_Display hex_digit_display_1 (.value(\六十进制计数器_1_q1a ));  // open: dp
  Hex_Digit_Display hex_digit_display_2 (.value(\六十进制计数器_1_q0a ));  // open: dp
  Button button_3 (.out(button_3_out));
  Hex_Digit_Display hex_digit_display_3 (.value(\六十进制计数器_2_q1a ));  // open: dp
  \六十进制计数器  \u_六十进制计数器_2  (
    .Adj(in_2), .Q0d(\六十进制计数器_2_q0a [3]), .Q0c(\六十进制计数器_2_q0a [2]), .Q0b(\六十进制计数器_2_q0a [1]),
    .Q0a(\六十进制计数器_2_q0a [0]), .Q1d(\六十进制计数器_2_q1a [3]), .Q1c(\六十进制计数器_2_q1a [2]), .Q1b(\六十进制计数器_2_q1a [1]),
    .Q1a(\六十进制计数器_2_q1a [0]), .Clr(in_4), .CPU(\六十进制计数器_1_nqcc ), .CPD(button_3_out));  // open: nQcc
  Hex_Digit_Display hex_digit_display_4 (.value(\六十进制计数器_2_q0a ));  // open: dp
endmodule

module \十二进制计数器或二十四进制的计数器电路  (
  input  in_1,
  input  in_2,
  input  in_3,
  input  in_4,
  input  in_5,
  output out_6,
  output out_7,
  output out_8,
  output out_9,
  output out_10,
  output out_11,
  output out_12,
  output out_13,
  output out_14
);

  wire and_1_out, and_2_out, not_1_out, or_1_out;

  \六十进制计数器  \u_六十进制计数器_1  (
    .Adj(in_3), .Q0d(out_10), .Q0c(out_11), .Q0b(out_12), .Q0a(out_13), .Q1d(out_6), .Q1c(out_7),
    .Q1b(out_8), .Q1a(out_9), .Clr(or_1_out), .CPU(in_2), .CPD(in_4));  // open: nQcc
  not not_1 (not_1_out, in_1);
  or or_1 (or_1_out, out_14, in_5);
  and and_1 (and_1_out, out_9, out_12, not_1_out);
  and and_2 (and_2_out, out_8, out_11, in_1);
  or or_2 (out_14, and_2_out, and_1_out);
endmodule

module \十二进制计数器或二十四进制的计数器测试电路  (
  input  in_1,
  input  in_2,
  input  in_3,
  input  in_4,
  input  in_5,
  input  in_6
);

  wire button_1_out, button_2_out, button_3_out, \十二进制计数器或二十四进制的计数器电路_1_out_14 ;
  wire [3:0] \十二进制计数器或二十四进制的计数器电路_1_out_9 , \十二进制计数器或二十四进制的计数器电路_1_out_13 , \十二进制计数器或二十四进制的计数器电路_2_out_9 ,
       \十二进制计数器或二十四进制的计数器电路_2_out_13 ;

  Button button_1 (.out(button_1_out));
  Button button_2 (.out(button_2_out));
  Hex_Digit_Display hex_digit_display_1 (.value(\十二进制计数器或二十四进制的计数器电路_1_out_9 ));  // open: dp
  Hex_Digit_Display hex_digit_display_2 (.value(\十二进制计数器或二十四进制的计数器电路_1_out_13 ));  // open: dp
  \十二进制计数器或二十四进制的计数器电路  \u_十二进制计数器或二十四进制的计数器电路_1  (
    .in_3(in_1), .out_14(\十二进制计数器或二十四进制的计数器电路_1_out_14 ), .out_6(\十二进制计数器或二十四进制的计数器电路_1_out_9 [3]),
    .out_7(\十二进制计数器或二十四进制的计数器电路_1_out_9 [2]), .out_8(\十二进制计数器或二十四进制的计数器电路_1_out_9 [1]),
    .out_9(\十二进制计数器或二十四进制的计数器电路_1_out_9 [0]), .out_10(\十二进制计数器或二十四进制的计数器电路_1_out_13 [3]),
    .out_11(\十二进制计数器或二十四进制的计数器电路_1_out_13 [2]), .out_12(\十二进制计数器或二十四进制的计数器电路_1_out_13 [1]),
    .out_13(\十二进制计数器或二十四进制的计数器电路_1_out_13 [0]), .in_1(in_2), .in_2(button_1_out), .in_4(button_2_out),
    .in_5(in_5));
  Button button_3 (.out(button_3_out));
  Hex_Digit_Display hex_digit_display_3 (.value(\十二进制计数器或二十四进制的计数器电路_2_out_9 ));  // open: dp
  Hex_Digit_Display hex_digit_display_4 (.value(\十二进制计数器或二十四进制的计数器电路_2_out_13 ));  // open: dp
  \十二进制计数器或二十四进制的计数器电路  \u_十二进制计数器或二十四进制的计数器电路_2  (
    .in_3(in_3), .out_6(\十二进制计数器或二十四进制的计数器电路_2_out_9 [3]), .out_7(\十二进制计数器或二十四进制的计数器电路_2_out_9 [2]),
    .out_8(\十二进制计数器或二十四进制的计数器电路_2_out_9 [1]), .out_9(\十二进制计数器或二十四进制的计数器电路_2_out_9 [0]),
    .out_10(\十二进制计数器或二十四进制的计数器电路_2_out_13 [3]), .out_11(\十二进制计数器或二十四进制的计数器电路_2_out_13 [2]),
    .out_12(\十二进制计数器或二十四进制的计数器电路_2_out_13 [1]), .out_13(\十二进制计数器或二十四进制的计数器电路_2_out_13 [0]), .in_1(in_4),
    .in_2(\十二进制计数器或二十四进制的计数器电路_1_out_14 ), .in_4(button_3_out), .in_5(in_6));  // open: out_14
endmodule

module \上下午文字显示测试电路  (
  input  in_1,
  input  in_2
);

  wire [4:0] \上下午文字显示的电路_1_out_3 , \上下午文字显示的电路_1_out_4 , \上下午文字显示的电路_1_out_5 , \上下午文字显示的电路_1_out_6 ;

  DotMatrix #(.inputtype("column"), .matrixcols(4), .matrixrows(5), .persist(0), .dotshape("square")) dotmatrix_1 (
    .col0(\上下午文字显示的电路_1_out_3 ), .col1(\上下午文字显示的电路_1_out_4 ), .col2(\上下午文字显示的电路_1_out_5 ),
    .col3(\上下午文字显示的电路_1_out_6 ));
  \上下午文字显示的电路  \u_上下午文字显示的电路_1  (
    .in_1(in_1), .in_2(in_2), .out_3(\上下午文字显示的电路_1_out_3 ), .out_4(\上下午文字显示的电路_1_out_4 ),
    .out_5(\上下午文字显示的电路_1_out_5 ), .out_6(\上下午文字显示的电路_1_out_6 ));
endmodule

module \上下午文字显示的电路  (
  input  in_1,
  input  in_2,
  output [4:0] out_3,
  output [4:0] out_4,
  output [4:0] out_5,
  output [4:0] out_6
);

  wire not_1_out, not_2_out;

  and and_1 (out_4[4], not_1_out, in_2);
  not not_1 (not_1_out, 1'b0);
  and and_2 (out_3[0], not_2_out, in_2);
  not not_2 (not_2_out, in_1);
  and and_3 (out_3[4], in_1, in_2);

  assign out_3[3:1] = 3'b000;
  assign out_4[3:0] = {4{out_4[4]}};
  assign out_5 = {out_3[4], 1'b0, out_4[4], 1'b0, out_3[0]};
  assign out_6 = {out_3[4], 3'b000, out_3[0]};
endmodule

module \电子钟整点报时电路  (
  input  in_1,
  input  in_2,
  input  in_3,
  input  in_4,
  input  in_5,
  input  in_6,
  input  in_7,
  input  in_8,
  input  in_9,
  input  in_10,
  input  in_11,
  input  in_12,
  input  in_13,
  output out_14
);

  wire and_1_out, and_2_out, and_3_out, and_4_out, not_1_out, not_2_out, not_3_out, not_4_out, not_5_out,
       not_6_out;

  not not_1 (not_1_out, in_2);
  and and_1 (and_1_out, not_1_out, in_3, not_2_out, in_5);
  not not_2 (not_2_out, in_4);
  and and_2 (and_2_out, and_1_out, and_3_out, and_4_out);
  and and_3 (and_3_out, in_6, not_3_out, not_4_out, in_9);
  not not_3 (not_3_out, in_7);
  D_Flip_Flop #(.trigger("falling"), .Pre_Clr_Positions("LEGACY"), .NegatePresetClear("false"), .enable("false"), .NewFFLayout("false")) d_ff_1 (
    .clk(in_1), .D(and_2_out), .Q(out_14));  // open: Qn, preset, reset
  not not_4 (not_4_out, in_8);
  not not_5 (not_5_out, in_10);
  and and_4 (and_4_out, not_5_out, in_11, not_6_out, in_13);
  not not_6 (not_6_out, in_12);
endmodule

module \电子钟整点报时电路测试电路  (
  input  Adj
);

  wire Clk_out, Min_0_out, Min_minus_out, Min_plus_out, or_1_out, or_2_out, Sec_0_out, Sec_minus_out,
       Sec_plus_out, \六十进制计数器_1_nqcc , \六十进制计数器_1_q1a , \六十进制计数器_1_q1b , \六十进制计数器_1_q1c , \六十进制计数器_1_q1d ,
       \六十进制计数器_2_q0a , \六十进制计数器_2_q0b , \六十进制计数器_2_q0c , \六十进制计数器_2_q0d , \六十进制计数器_2_q1a , \六十进制计数器_2_q1b ,
       \六十进制计数器_2_q1c , \六十进制计数器_2_q1d , \电子钟整点报时电路_1_out_14 ;

  Clock #(.highDuration(1), .lowDuration(1)) Clk (.out(Clk_out));
  Button Sec_plus (.out(Sec_plus_out));
  Button Sec_minus (.out(Sec_minus_out));
  Button Min_plus (.out(Min_plus_out));
  Button Min_minus (.out(Min_minus_out));
  or or_1 (or_1_out, Sec_plus_out, Clk_out);
  \六十进制计数器  \u_六十进制计数器_1  (
    .Adj(Adj), .nQcc(\六十进制计数器_1_nqcc ), .Q1d(\六十进制计数器_1_q1d ), .Q1c(\六十进制计数器_1_q1c ), .Q1b(\六十进制计数器_1_q1b ),
    .Q1a(\六十进制计数器_1_q1a ), .Clr(Sec_0_out), .CPU(or_1_out), .CPD(Sec_minus_out));  // open: Q0d, Q0c, Q0b, Q0a
  Button Sec_0 (.out(Sec_0_out));
  or or_2 (or_2_out, \六十进制计数器_1_nqcc , Min_plus_out);
  \电子钟整点报时电路  \u_电子钟整点报时电路_1  (
    .out_14(\电子钟整点报时电路_1_out_14 ), .in_2(\六十进制计数器_2_q1d ), .in_3(\六十进制计数器_2_q1c ), .in_4(\六十进制计数器_2_q1b ),
    .in_5(\六十进制计数器_2_q1a ), .in_6(\六十进制计数器_2_q0d ), .in_1(Clk_out), .in_7(\六十进制计数器_2_q0c ),
    .in_8(\六十进制计数器_2_q0b ), .in_9(\六十进制计数器_2_q0a ), .in_10(\六十进制计数器_1_q1d ), .in_11(\六十进制计数器_1_q1c ),
    .in_12(\六十进制计数器_1_q1b ), .in_13(\六十进制计数器_1_q1a ));
  \六十进制计数器  \u_六十进制计数器_2  (
    .Adj(Adj), .Q0d(\六十进制计数器_2_q0d ), .Q0c(\六十进制计数器_2_q0c ), .Q0b(\六十进制计数器_2_q0b ), .Q0a(\六十进制计数器_2_q0a ),
    .Q1d(\六十进制计数器_2_q1d ), .Q1c(\六十进制计数器_2_q1c ), .Q1b(\六十进制计数器_2_q1b ), .Q1a(\六十进制计数器_2_q1a ),
    .Clr(Min_0_out), .CPU(or_2_out), .CPD(Min_minus_out));  // open: nQcc
  LED #(.active("true")) led_1 (.in(\电子钟整点报时电路_1_out_14 ));
  Button Min_0 (.out(Min_0_out));
endmodule

module \秒脉冲产生电路  (
  input  in_1,
  output out_2
);

  \四位二进制可逆计数器  \u_四位二进制可逆计数器_1  (
    .CPD(1'b0), .CPU(in_1), .A(1'b0), .B(1'b0), .C(1'b0), .QD(out_2), .D(1'b0), .nLD(1'b1), .CLR(out_2));  // open: QA, QB, QC
endmodule

module \多功能数字钟  (
  input  in_1,
  input  in_2,
  input  in_3,
  input  in_4,
  input  in_5,
  input  in_6,
  input  in_7,
  input  in_8,
  input  Set,
  input  Adj0,
  input  Adj1,
  input  Clr,
  input  CPU,
  input  CPD,
  output [4:0] out_15,
  output [4:0] out_16,
  output [4:0] out_17,
  output [4:0] out_18,
  output out_19,
  output [3:0] out_20,
  output [3:0] out_21,
  output [3:0] out_22,
  output [3:0] out_23,
  output [3:0] out_24,
  output [3:0] out_25,
  output [3:0] out_26,
  output out_27,
  output [3:0] out_28,
  output [3:0] out_29,
  output [3:0] out_30,
  output [3:0] out_31,
  output [3:0] out_32
);

  wire and_1_out, and_2_out, and_5_out, and_7_out, and_8_out, not_1_out, not_2_out, not_3_out, not_4_out,
       not_5_out, not_6_out, or_1_out, or_2_out, t_ff_1_q, \六十进制计数器_1_nqcc , \六十进制计数器_2_nqcc ,
       \十二进制计数器或二十四进制的计数器电路_1_out_14 , \秒脉冲产生电路_1_out_2 ;

  \秒脉冲产生电路  \u_秒脉冲产生电路_1  (.out_2(\秒脉冲产生电路_1_out_2 ), .in_1(in_8));
  not not_1 (not_1_out, Adj1);
  and and_1 (and_1_out, CPU, not_1_out, Adj0);
  or or_1 (or_1_out, and_1_out, \六十进制计数器_1_nqcc );
  and and_2 (and_2_out, not_1_out, Adj0, CPD);
  \十二进制计数器或二十四进制的计数器电路  \u_十二进制计数器或二十四进制的计数器电路_1  (
    .in_3(Adj0), .out_14(\十二进制计数器或二十四进制的计数器电路_1_out_14 ), .out_6(out_28[3]), .out_7(out_28[2]),
    .out_8(out_28[1]), .out_9(out_28[0]), .out_10(out_29[3]), .out_11(out_29[2]), .out_12(out_29[1]),
    .out_13(out_29[0]), .in_1(Set), .in_2(or_1_out), .in_4(and_2_out), .in_5(Clr));
  and and_3 (out_16[4], not_2_out, not_5_out);
  not not_2 (not_2_out, 1'b0);
  and and_4 (out_15[0], not_3_out, not_5_out);
  not not_3 (not_3_out, t_ff_1_q);
  T_Flip_Flop #(.trigger("rising"), .Pre_Clr_Positions("LEGACY"), .NegatePresetClear("false"), .enable("false"), .NewFFLayout("false")) t_ff_1 (
    .clk(\十二进制计数器或二十四进制的计数器电路_1_out_14 ), .T(1'b1), .Q(t_ff_1_q), .preset(not_4_out), .reset(not_4_out));  // open: Qn
  not not_4 (not_4_out, 1'b1);
  and and_5 (and_5_out, CPU, Adj1, Adj0);
  and and_6 (out_15[4], t_ff_1_q, not_5_out);
  not not_5 (not_5_out, Set);
  \六十进制计数器  \u_六十进制计数器_1  (
    .Adj(Adj0), .Q0d(out_30[3]), .Q0c(out_30[2]), .Q0b(out_30[1]), .Q0a(out_30[0]), .nQcc(\六十进制计数器_1_nqcc ),
    .Q1d(out_26[3]), .Q1c(out_26[2]), .Q1b(out_26[1]), .Q1a(out_26[0]), .Clr(Clr), .CPU(or_2_out),
    .CPD(and_7_out));
  or or_2 (or_2_out, and_5_out, \六十进制计数器_2_nqcc );
  and and_7 (and_7_out, Adj1, Adj0, CPD);
  and and_8 (and_8_out, \秒脉冲产生电路_1_out_2 , not_6_out);
  not not_6 (not_6_out, Adj0);
  \电子钟整点报时电路  \u_电子钟整点报时电路_1  (
    .out_14(out_19), .in_2(out_26[3]), .in_3(out_26[2]), .in_4(out_26[1]), .in_5(out_26[0]),
    .in_6(out_30[3]), .in_1(\秒脉冲产生电路_1_out_2 ), .in_7(out_30[2]), .in_8(out_30[1]), .in_9(out_30[0]),
    .in_10(out_31[3]), .in_11(out_31[2]), .in_12(out_31[1]), .in_13(out_31[0]));
  \六十进制计数器  \u_六十进制计数器_2  (
    .Adj(Adj0), .Q0d(out_32[3]), .Q0c(out_32[2]), .Q0b(out_32[1]), .Q0a(out_32[0]), .nQcc(\六十进制计数器_2_nqcc ),
    .Q1d(out_31[3]), .Q1c(out_31[2]), .Q1b(out_31[1]), .Q1a(out_31[0]), .Clr(Clr), .CPU(and_8_out), .CPD(1'b0));
  \闹钟  \u_闹钟_1  (
    .out_18(out_20[3]), .out_24(out_20[2]), .out_30(out_20[1]), .out_36(out_20[0]), .out_19(out_21[3]),
    .out_25(out_21[2]), .out_31(out_21[1]), .out_37(out_21[0]), .out_20(out_22[3]), .out_26(out_22[2]),
    .out_32(out_22[1]), .out_38(out_22[0]), .out_21(out_23[3]), .out_27(out_23[2]), .out_33(out_23[1]),
    .out_39(out_23[0]), .out_17(out_27), .out_22(out_24[3]), .out_28(out_24[2]), .out_34(out_24[1]),
    .out_40(out_24[0]), .out_23(out_25[3]), .out_29(out_25[2]), .out_35(out_25[1]), .out_41(out_25[0]),
    .in_8(in_1), .in_9(in_2), .in_10(in_3), .in_11(in_4), .in_12(in_5), .in_13(in_6), .in_14(1'b0),
    .in_15(1'b0), .in_16(1'b0), .in_1(in_7), .in_4(out_26), .in_6(out_28), .in_5(out_30), .in_7(out_29),
    .in_3(out_31), .in_2(\秒脉冲产生电路_1_out_2 ));

  assign out_15[3:1] = 3'b000;
  assign out_16[3:0] = {4{out_16[4]}};
  assign out_17 = {out_15[4], 1'b0, out_16[4], 1'b0, out_15[0]};
  assign out_18 = {out_15[4], 3'b000, out_15[0]};
endmodule

module \多功能数字钟测试电路  (
  input  in_1,
  input  in_2,
  input  in_3,
  input  in_4
);

  wire button_1_out, button_2_out, button_3_out, button_4_out, button_5_out, button_6_out, button_7_out,
       button_8_out, clock_1_out, switch_1_p2, \多功能数字钟_1_out_19 , \多功能数字钟_1_out_27 ;
  wire [3:0] \多功能数字钟_1_out_20 , \多功能数字钟_1_out_21 , \多功能数字钟_1_out_22 , \多功能数字钟_1_out_23 , \多功能数字钟_1_out_24 ,
       \多功能数字钟_1_out_25 , \多功能数字钟_1_out_26 , \多功能数字钟_1_out_28 , \多功能数字钟_1_out_29 , \多功能数字钟_1_out_30 ,
       \多功能数字钟_1_out_31 , \多功能数字钟_1_out_32 ;
  wire [4:0] \多功能数字钟_1_out_15 , \多功能数字钟_1_out_16 , \多功能数字钟_1_out_17 , \多功能数字钟_1_out_18 ;

  DotMatrix #(.inputtype("column"), .matrixcols(4), .matrixrows(5), .persist(0), .dotshape("square")) dotmatrix_1 (
    .col0(\多功能数字钟_1_out_15 ), .col1(\多功能数字钟_1_out_16 ), .col2(\多功能数字钟_1_out_17 ), .col3(\多功能数字钟_1_out_18 ));
  Hex_Digit_Display hex_digit_display_1 (.value(\多功能数字钟_1_out_28 ));  // open: dp
  \多功能数字钟  \u_多功能数字钟_1  (
    .in_8(clock_1_out), .Set(in_3), .Adj0(in_1), .Adj1(in_2), .Clr(in_4), .CPU(button_2_out),
    .CPD(button_1_out), .out_28(\多功能数字钟_1_out_28 ), .out_29(\多功能数字钟_1_out_29 ), .out_26(\多功能数字钟_1_out_26 ),
    .out_30(\多功能数字钟_1_out_30 ), .out_31(\多功能数字钟_1_out_31 ), .out_32(\多功能数字钟_1_out_32 ),
    .out_15(\多功能数字钟_1_out_15 ), .out_16(\多功能数字钟_1_out_16 ), .out_17(\多功能数字钟_1_out_17 ),
    .out_18(\多功能数字钟_1_out_18 ), .out_19(\多功能数字钟_1_out_19 ), .out_27(\多功能数字钟_1_out_27 ),
    .out_20(\多功能数字钟_1_out_20 ), .out_21(\多功能数字钟_1_out_21 ), .out_22(\多功能数字钟_1_out_22 ),
    .out_23(\多功能数字钟_1_out_23 ), .out_24(\多功能数字钟_1_out_24 ), .out_25(\多功能数字钟_1_out_25 ), .in_7(switch_1_p2),
    .in_1(button_3_out), .in_2(button_5_out), .in_3(button_6_out), .in_4(button_4_out), .in_5(button_7_out),
    .in_6(button_8_out));
  Clock #(.highDuration(1), .lowDuration(1)) clock_1 (.out(clock_1_out));
  Button button_1 (.out(button_1_out));
  Button button_2 (.out(button_2_out));
  Hex_Digit_Display hex_digit_display_2 (.value(\多功能数字钟_1_out_29 ));  // open: dp
  Hex_Digit_Display hex_digit_display_3 (.value(\多功能数字钟_1_out_26 ));  // open: dp
  Hex_Digit_Display hex_digit_display_4 (.value(\多功能数字钟_1_out_30 ));  // open: dp
  Button button_3 (.out(button_3_out));
  Button button_4 (.out(button_4_out));
  Button button_5 (.out(button_5_out));
  Button button_6 (.out(button_6_out));
  Hex_Digit_Display hex_digit_display_5 (.value(\多功能数字钟_1_out_31 ));  // open: dp
  Hex_Digit_Display hex_digit_display_6 (.value(\多功能数字钟_1_out_32 ));  // open: dp
  Button button_7 (.out(button_7_out));
  Button button_8 (.out(button_8_out));
  LED #(.active("true")) led_1 (.in(\多功能数字钟_1_out_27 ));
  LED #(.active("true")) led_2 (.in(\多功能数字钟_1_out_19 ));
  // Switch #(.width(1)) switch_1: pin names not known; wires that end beside it: 1'b1, switch_1_p2
  Hex_Digit_Display hex_digit_display_7 (.value(\多功能数字钟_1_out_21 ));  // open: dp
  Hex_Digit_Display hex_digit_display_8 (.value(\多功能数字钟_1_out_20 ));  // open: dp
  Hex_Digit_Display hex_digit_display_9 (.value(\多功能数字钟_1_out_23 ));  // open: dp
  Hex_Digit_Display hex_digit_display_10 (.value(\多功能数字钟_1_out_22 ));  // open: dp
  Hex_Digit_Display hex_digit_display_11 (.value(\多功能数字钟_1_out_24 ));  // open: dp
  Hex_Digit_Display hex_digit_display_12 (.value(\多功能数字钟_1_out_25 ));  // open: dp
endmodule

module \闹钟  (
  input  in_1,
  input  in_2,
  input  [3:0] in_3,
  input  [3:0] in_4,
  input  [3:0] in_5,
  input  [3:0] in_6,
  input  [3:0] in_7,
  input  in_8,
  input  in_9,
  input  in_10,
  input  in_11,
  input  in_12,
  input  in_13,
  input  in_14,
  input  in_15,
  input  in_16,
  output out_17,
  output out_18,
  output out_19,
  output out_20,
  output out_21,
  output out_22,
  output out_23,
  output out_24,
  output out_25,
  output out_26,
  output out_27,
  output out_28,
  output out_29,
  output out_30,
  output out_31,
  output out_32,
  output out_33,
  output out_34,
  output out_35,
  output out_36,
  output out_37,
  output out_38,
  output out_39,
  output out_40,
  output out_41
);

  wire and_1_out, and_2_out, and_3_out, and_4_out, and_5_out, and_6_out, d_ff_1_q, not_1_out, or_1_out,
       or_2_out, or_3_out, xnor_1_out, xnor_2_out, xnor_3_out, xnor_4_out, xnor_5_out, xnor_6_out,
       xnor_7_out, xnor_8_out, xnor_9_out, xnor_10_out, xnor_11_out, xnor_12_out, xnor_13_out, xnor_14_out,
       xnor_15_out, xnor_16_out, \六十进制计数器_1_nqcc , \六十进制计数器_2_nqcc ;

  xnor xnor_1 (xnor_1_out, in_4[2], out_24);
  xnor xnor_2 (xnor_2_out, in_4[3], out_18);
  and and_1 (and_1_out, xnor_2_out, xnor_1_out, xnor_3_out, xnor_4_out);
  xnor xnor_3 (xnor_3_out, in_4[1], out_30);
  xnor xnor_4 (xnor_4_out, in_4[0], in_6[3]);
  xnor xnor_5 (xnor_5_out, in_6[3], out_19);
  and and_2 (and_2_out, and_1_out, and_3_out);
  and and_3 (and_3_out, xnor_5_out, xnor_7_out, xnor_6_out, xnor_8_out);
  xnor xnor_6 (xnor_6_out, in_6[3], out_31);
  xnor xnor_7 (xnor_7_out, in_6[3], out_25);
  xnor xnor_8 (xnor_8_out, in_6[3], out_37);
  or or_1 (or_1_out, in_8, \六十进制计数器_1_nqcc );
  \十二进制计数器或二十四进制的计数器电路  \u_十二进制计数器或二十四进制的计数器电路_1  (
    .in_3(1'b1), .out_6(out_18), .out_7(out_24), .out_8(out_30), .out_9(in_6[3]), .out_10(out_19),
    .out_11(out_25), .out_12(out_31), .out_13(out_37), .in_1(1'b1), .in_2(or_1_out), .in_4(in_9), .in_5(in_10));  // open: out_14
  xnor xnor_9 (xnor_9_out, in_5[3], out_20);
  xnor xnor_10 (xnor_10_out, in_5[2], out_26);
  and and_4 (and_4_out, xnor_9_out, xnor_10_out, xnor_11_out, xnor_12_out);
  xnor xnor_11 (xnor_11_out, in_5[1], out_32);
  xnor xnor_12 (xnor_12_out, in_5[0], out_38);
  xnor xnor_13 (xnor_13_out, in_7[3], out_21);
  and and_5 (and_5_out, and_4_out, and_6_out);
  and and_6 (and_6_out, xnor_13_out, xnor_15_out, xnor_14_out, xnor_16_out);
  xnor xnor_14 (xnor_14_out, in_7[1], out_33);
  xnor xnor_15 (xnor_15_out, in_7[2], out_27);
  xnor xnor_16 (xnor_16_out, in_7[0], out_39);
  \六十进制计数器  \u_六十进制计数器_1  (
    .Adj(1'b1), .Q0d(out_21), .Q0c(out_27), .Q0b(out_33), .Q0a(out_39), .nQcc(\六十进制计数器_1_nqcc ),
    .Q1d(out_20), .Q1c(out_26), .Q1b(out_32), .Q1a(out_38), .Clr(in_13), .CPU(or_2_out), .CPD(in_12));
  or or_2 (or_2_out, in_11, \六十进制计数器_2_nqcc );
  not not_1 (not_1_out, or_3_out);
  or or_3 (or_3_out, in_3[3], in_3[2], in_3[1], in_3[0]);
  and and_7 (out_17, and_2_out, and_5_out, d_ff_1_q, in_1);
  D_Flip_Flop #(.trigger("falling"), .Pre_Clr_Positions("LEGACY"), .NegatePresetClear("false"), .enable("false"), .NewFFLayout("false")) d_ff_1 (
    .clk(in_2), .D(not_1_out), .Q(d_ff_1_q));  // open: Qn, preset, reset
  \六十进制计数器  \u_六十进制计数器_2  (
    .Adj(1'b1), .Q0d(out_23), .Q0c(out_29), .Q0b(out_35), .Q0a(out_41), .nQcc(\六十进制计数器_2_nqcc ),
    .Q1d(out_22), .Q1c(out_28), .Q1b(out_34), .Q1a(out_40), .Clr(in_16), .CPU(in_14), .CPD(in_15));

  assign in_6[2:0] = {3{in_6[3]}};
  assign out_36 = in_6[3];
endmodule

module \闹钟测试  (
  input  [3:0] in_1,
  input  [3:0] in_2,
  input  [3:0] in_3,
  input  [3:0] in_4,
  input  [3:0] in_5,
  input  [3:0] in_6,
  input  in_7
);

  wire button_1_out, button_2_out, button_3_out, button_4_out, button_5_out, button_6_out, button_7_out,
       button_8_out, button_9_out, switch_1_p2, \闹钟_1_out_17 ;
  wire [3:0] \闹钟_1_out_36 , \闹钟_1_out_37 , \闹钟_1_out_38 , \闹钟_1_out_39 , \闹钟_1_out_40 , \闹钟_1_out_41 ;

  Hex_Digit_Display hex_digit_display_1 (.value(in_1));  // open: dp
  Hex_Digit_Display hex_digit_display_2 (.value(in_2));  // open: dp
  Hex_Digit_Display hex_digit_display_3 (.value(in_3));  // open: dp
  Hex_Digit_Display hex_digit_display_4 (.value(in_4));  // open: dp
  Hex_Digit_Display hex_digit_display_5 (.value(in_5));  // open: dp
  Hex_Digit_Display hex_digit_display_6 (.value(in_6));  // open: dp
  Hex_Digit_Display hex_digit_display_7 (.value(\闹钟_1_out_36 ));  // open: dp
  Hex_Digit_Display hex_digit_display_8 (.value(\闹钟_1_out_38 ));  // open: dp
  Hex_Digit_Display hex_digit_display_9 (.value(\闹钟_1_out_37 ));  // open: dp
  Button button_1 (.out(button_1_out));
  Button button_2 (.out(button_2_out));
  Button button_3 (.out(button_3_out));
  Hex_Digit_Display hex_digit_display_10 (.value(\闹钟_1_out_39 ));  // open: dp
  Button button_4 (.out(button_4_out));
  Button button_5 (.out(button_5_out));
  Button button_6 (.out(button_6_out));
  Hex_Digit_Display hex_digit_display_11 (.value(\闹钟_1_out_40 ));  // open: dp
  Hex_Digit_Display hex_digit_display_12 (.value(\闹钟_1_out_41 ));  // open: dp
  Button button_7 (.out(button_7_out));
  Button button_8 (.out(button_8_out));
  Button button_9 (.out(button_9_out));
  \闹钟  \u_闹钟_1  (
    .out_18(\闹钟_1_out_36 [3]), .out_24(\闹钟_1_out_36 [2]), .out_30(\闹钟_1_out_36 [1]),
    .out_36(\闹钟_1_out_36 [0]), .out_19(\闹钟_1_out_37 [3]), .out_25(\闹钟_1_out_37 [2]),
    .out_31(\闹钟_1_out_37 [1]), .out_37(\闹钟_1_out_37 [0]), .out_20(\闹钟_1_out_38 [3]),
    .out_26(\闹钟_1_out_38 [2]), .out_32(\闹钟_1_out_38 [1]), .out_38(\闹钟_1_out_38 [0]),
    .out_21(\闹钟_1_out_39 [3]), .out_27(\闹钟_1_out_39 [2]), .out_33(\闹钟_1_out_39 [1]),
    .out_39(\闹钟_1_out_39 [0]), .out_17(\闹钟_1_out_17 ), .out_22(\闹钟_1_out_40 [3]), .out_28(\闹钟_1_out_40 [2]),
    .out_34(\闹钟_1_out_40 [1]), .out_40(\闹钟_1_out_40 [0]), .out_23(\闹钟_1_out_41 [3]),
    .out_29(\闹钟_1_out_41 [2]), .out_35(\闹钟_1_out_41 [1]), .out_41(\闹钟_1_out_41 [0]), .in_8(button_1_out),
    .in_9(button_2_out), .in_10(button_3_out), .in_11(button_4_out), .in_12(button_5_out),
    .in_13(button_6_out), .in_14(button_9_out), .in_15(button_7_out), .in_16(button_8_out),
    .in_1(switch_1_p2), .in_4(in_4), .in_6(in_1), .in_5(in_5), .in_7(in_2), .in_3(in_5), .in_2(in_7));
  // Switch #(.width(1)) switch_1: pin names not known; wires that end beside it: 1'b1, switch_1_p2
  LED #(.active("true")) led_1 (.in(\闹钟_1_out_17 ));
endmodule
