// Logisim project 实验6-CS200X-0618-Yuigahama.circ as structural Verilog: 7 circuits, main circuit sqrX
module sqrX (
  input  [31:0] in_1,
  input  [31:0] in_2,
  input  [31:0] in_3,
  input  [31:0] in_4,
  output [31:0] out_5,
  output [31:0] out_6,
  output [31:0] out_7,
  output [31:0] out_8
);

  wire [31:0] multiplier_1_out, multiplier_2_out, multiplier_3_out, multiplier_4_out, multiplier_5_out,
       multiplier_6_out, multiplier_7_out, multiplier_8_out;

  Multiplier #(.width(32)) multiplier_1 (.a(in_1), .b(in_1), .out(multiplier_1_out));  // open: cin, cout
  Adder #(.width(32)) adder_1 (.a(multiplier_1_out), .b(multiplier_2_out), .out(out_5), .cin(1'b0));  // open: cout
  Multiplier #(.width(32)) multiplier_2 (.a(in_2), .b(in_3), .out(multiplier_2_out));  // open: cin, cout
  Multiplier #(.width(32)) multiplier_3 (.a(in_1), .b(in_2), .out(multiplier_3_out));  // open: cin, cout
  Adder #(.width(32)) adder_2 (.a(multiplier_3_out), .b(multiplier_4_out), .out(out_6), .cin(1'b0));  // open: cout
  Multiplier #(.width(32)) multiplier_4 (.a(in_2), .b(in_4), .out(multiplier_4_out));  // open: cin, cout
  Multiplier #(.width(32)) multiplier_5 (.a(in_1), .b(in_3), .out(multiplier_5_out));  // open: cin, cout
  Adder #(.width(32)) adder_3 (.a(multiplier_5_out), .b(multiplier_6_out), .out(out_7), .cin(1'b0));  // open: cout
  Multiplier #(.width(32)) multiplier_6 (.a(in_3), .b(in_4), .out(multiplier_6_out));  // open: cin, cout
  Multiplier #(.width(32)) multiplier_7 (.a(in_2), .b(in_3), .out(multiplier_7_out));  // open: cin, cout
  Adder #(.width(32)) adder_4 (.a(multiplier_7_out), .b(multiplier_8_out), .out(out_8), .cin(1'b0));  // open: cout
  Multiplier #(.width(32)) multiplier_8 (.a(in_4), .b(in_4), .out(multiplier_8_out));  // open: cin, cout
endmodule

module sqrX_A (
  input  [31:0] in_1,
  input  [31:0] in_2,
  input  [31:0] in_3,
  input  [31:0] in_4,
  output [31:0] out_5,
  output [31:0] out_6,
  output [31:0] out_7,
  output [31:0] out_8
);

  wire [31:0] adder_2_out, adder_4_out, multiplier_1_out, multiplier_2_out, multiplier_3_out,
       multiplier_4_out, multiplier_5_out, multiplier_6_out, multiplier_7_out, multiplier_8_out;

  Multiplier #(.width(32)) multiplier_1 (.a(in_1), .b(in_2), .out(multiplier_1_out));  // open: cin, cout
  Adder #(.width(32)) adder_1 (.a(multiplier_1_out), .b(multiplier_2_out), .out(out_5), .cin(1'b0));  // open: cout
  Multiplier #(.width(32)) multiplier_2 (.a(in_2), .b(in_4), .out(multiplier_2_out));  // open: cin, cout
  Multiplier #(.width(32)) multiplier_3 (.a(in_1), .b(in_1), .out(multiplier_3_out));  // open: cin, cout
  Adder #(.width(32)) adder_2 (
    .a(multiplier_3_out), .b(multiplier_4_out), .out(adder_2_out), .cin(1'b0));  // open: cout
  Multiplier #(.width(32)) multiplier_4 (.a(in_2), .b(in_3), .out(multiplier_4_out));  // open: cin, cout
  Multiplier #(.width(32)) multiplier_5 (.a(in_2), .b(in_3), .out(multiplier_5_out));  // open: cin, cout
  Adder #(.width(32)) adder_3 (.a(multiplier_5_out), .b(multiplier_6_out), .out(out_7), .cin(1'b0));  // open: cout
  Multiplier #(.width(32)) multiplier_6 (.a(in_4), .b(in_4), .out(multiplier_6_out));  // open: cin, cout
  Multiplier #(.width(32)) multiplier_7 (.a(in_1), .b(in_3), .out(multiplier_7_out));  // open: cin, cout
  Adder #(.width(32)) adder_4 (
    .a(multiplier_7_out), .b(multiplier_8_out), .out(adder_4_out), .cin(1'b0));  // open: cout
  Multiplier #(.width(32)) multiplier_8 (.a(in_3), .b(in_4), .out(multiplier_8_out));  // open: cin, cout
  Adder #(.width(32)) adder_5 (.a(out_5), .b(adder_2_out), .out(out_6), .cin(1'b0));  // open: cout
  Adder #(.width(32)) adder_6 (.a(out_7), .b(adder_4_out), .out(out_8), .cin(1'b0));  // open: cout
endmodule

module \Fibonacci数显示模块  (
  input  [31:0] in_1,
  output [3:0] out_2,
  output [3:0] out_3,
  output [3:0] out_4,
  output [3:0] out_5,
  output [3:0] out_6,
  output [3:0] out_7,
  output [3:0] out_8,
  output [3:0] out_9,
  output [3:0] out_10,
  output [3:0] out_11
);

  wire [31:0] divider_1_out, divider_2_out, divider_3_out, divider_4_out, divider_5_out, divider_6_out,
       divider_7_out, divider_8_out, divider_9_out;
  wire [31:4] divider_1_rem, divider_2_rem, divider_3_rem, divider_4_rem, divider_5_rem, divider_6_rem,
       divider_7_rem, divider_8_rem, divider_9_rem, divider_10_rem;

  Divider #(.width(32)) divider_1 (
    .a(in_1), .b(32'ha), .out(divider_1_out), .upper({32{1'b0}}), .rem({divider_1_rem, out_2}));
  Divider #(.width(32)) divider_2 (
    .a(divider_9_out), .b(32'ha), .out(divider_2_out), .upper({32{1'b0}}), .rem({divider_2_rem, out_7}));
  Divider #(.width(32)) divider_3 (
    .a(divider_1_out), .b(32'ha), .out(divider_3_out), .upper({32{1'b0}}), .rem({divider_3_rem, out_3}));
  Divider #(.width(32)) divider_4 (
    .a(divider_2_out), .b(32'ha), .out(divider_4_out), .upper({32{1'b0}}), .rem({divider_4_rem, out_8}));
  Divider #(.width(32)) divider_5 (
    .a(divider_3_out), .b(32'ha), .out(divider_5_out), .upper({32{1'b0}}), .rem({divider_5_rem, out_4}));
  Divider #(.width(32)) divider_6 (
    .a(divider_4_out), .b(32'ha), .out(divider_6_out), .upper({32{1'b0}}), .rem({divider_6_rem, out_9}));
  Divider #(.width(32)) divider_7 (
    .a(divider_5_out), .b(32'ha), .out(divider_7_out), .upper({32{1'b0}}), .rem({divider_7_rem, out_5}));
  Divider #(.width(32)) divider_8 (
    .a(divider_6_out), .b(32'ha), .out(divider_8_out), .upper({32{1'b0}}), .rem({divider_8_rem, out_10}));
  Divider #(.width(32)) divider_9 (
    .a(divider_7_out), .b(32'ha), .out(divider_9_out), .upper({32{1'b0}}), .rem({divider_9_rem, out_6}));
  Divider #(.width(32)) divider_10 (
    .a(divider_8_out), .b(32'ha), .upper({32{1'b0}}), .rem({divider_10_rem, out_11}));  // open: out
endmodule

module \斐波那契_Fibonacci_数列计算器  (
  input  [5:0] in_1,
  input  in_2,
  input  in_3,
  output [3:0] out_4,
  output [3:0] out_5,
  output [3:0] out_6,
  output [3:0] out_7,
  output [3:0] out_8,
  output [3:0] out_9,
  output [3:0] out_10,
  output [3:0] out_11,
  output [3:0] out_12,
  output [3:0] out_13
);

  wire \控制器_1_clear_2 , \控制器_1_clock_2 , \控制器_1_ni_1 , \控制器_1_start ;
  wire [31:0] \矩阵快速幂算法迭代模块_1_bi_prime ;

  \控制器  \u_控制器_1  (
    .n(in_1), .Clock(in_3), .Clear(in_2), .ni_1(\控制器_1_ni_1 ), .Clock_2(\控制器_1_clock_2 ),
    .Start(\控制器_1_start ), .Clear_2(\控制器_1_clear_2 ));
  \矩阵快速幂算法迭代模块  \u_矩阵快速幂算法迭代模块_1  (
    .Start(\控制器_1_start ), .Clock(\控制器_1_clock_2 ), .Clr(\控制器_1_clear_2 ), .ni_1(\控制器_1_ni_1 ),
    .bi_prime(\矩阵快速幂算法迭代模块_1_bi_prime ));
  \Fibonacci数显示模块  \fibonacci数显示模块_1  (
    .in_1(\矩阵快速幂算法迭代模块_1_bi_prime ), .out_2(out_13), .out_7(out_8), .out_3(out_12), .out_8(out_7),
    .out_4(out_11), .out_9(out_6), .out_5(out_10), .out_10(out_5), .out_6(out_9), .out_11(out_4));
endmodule

module \斐波那契_Fibonacci_数列计算器验证电路  (
  input  [5:0] in_1
);

  wire button_1_out, button_2_out;
  wire [3:0] \斐波那契_fibonacci_数列计算器_1_out_4 , \斐波那契_fibonacci_数列计算器_1_out_5 , \斐波那契_fibonacci_数列计算器_1_out_6 ,
       \斐波那契_fibonacci_数列计算器_1_out_7 , \斐波那契_fibonacci_数列计算器_1_out_8 , \斐波那契_fibonacci_数列计算器_1_out_9 ,
       \斐波那契_fibonacci_数列计算器_1_out_10 , \斐波那契_fibonacci_数列计算器_1_out_11 , \斐波那契_fibonacci_数列计算器_1_out_12 ,
       \斐波那契_fibonacci_数列计算器_1_out_13 ;

  Button button_1 (.out(button_1_out));
  Button button_2 (.out(button_2_out));
  \斐波那契_Fibonacci_数列计算器  \u_斐波那契_fibonacci_数列计算器_1  (
    .in_1(in_1), .in_2(button_1_out), .in_3(button_2_out), .out_4(\斐波那契_fibonacci_数列计算器_1_out_4 ),
    .out_5(\斐波那契_fibonacci_数列计算器_1_out_5 ), .out_6(\斐波那契_fibonacci_数列计算器_1_out_6 ),
    .out_7(\斐波那契_fibonacci_数列计算器_1_out_7 ), .out_8(\斐波那契_fibonacci_数列计算器_1_out_8 ),
    .out_9(\斐波那契_fibonacci_数列计算器_1_out_9 ), .out_10(\斐波那契_fibonacci_数列计算器_1_out_10 ),
    .out_11(\斐波那契_fibonacci_数列计算器_1_out_11 ), .out_12(\斐波那契_fibonacci_数列计算器_1_out_12 ),
    .out_13(\斐波那契_fibonacci_数列计算器_1_out_13 ));
  Hex_Digit_Display hex_digit_display_1 (.value(\斐波那契_fibonacci_数列计算器_1_out_5 ));  // open: dp
  Hex_Digit_Display hex_digit_display_2 (.value(\斐波那契_fibonacci_数列计算器_1_out_4 ));  // open: dp
  Hex_Digit_Display hex_digit_display_3 (.value(\斐波那契_fibonacci_数列计算器_1_out_6 ));  // open: dp
  Hex_Digit_Display hex_digit_display_4 (.value(\斐波那契_fibonacci_数列计算器_1_out_7 ));  // open: dp
  Hex_Digit_Display hex_digit_display_5 (.value(\斐波那契_fibonacci_数列计算器_1_out_8 ));  // open: dp
  Hex_Digit_Display hex_digit_display_6 (.value(\斐波那契_fibonacci_数列计算器_1_out_10 ));  // open: dp
  Hex_Digit_Display hex_digit_display_7 (.value(\斐波那契_fibonacci_数列计算器_1_out_9 ));  // open: dp
  Hex_Digit_Display hex_digit_display_8 (.value(\斐波那契_fibonacci_数列计算器_1_out_11 ));  // open: dp
  Hex_Digit_Display hex_digit_display_9 (.value(\斐波那契_fibonacci_数列计算器_1_out_13 ));  // open: dp
  Hex_Digit_Display hex_digit_display_10 (.value(\斐波那契_fibonacci_数列计算器_1_out_12 ));  // open: dp
endmodule

module \矩阵快速幂算法迭代模块  (
  input  Start,
  input  Clock,
  input  Clr,
  input  ni_1,
  output [31:0] bi_prime
);

  wire [31:0] multiplexer_1_out, multiplexer_2_out, multiplexer_3_out, multiplexer_4_out, multiplexer_5_out,
       multiplexer_6_out, multiplexer_7_out, multiplexer_8_out, register_1_q, register_3_q, register_4_q,
       sqrx_1_out_5, sqrx_1_out_6, sqrx_1_out_7, sqrx_1_out_8, sqrx_a_1_out_5, sqrx_a_1_out_6,
       sqrx_a_1_out_7, sqrx_a_1_out_8;

  Multiplexer #(.select(1), .width(32), .disabled("Z"), .enable("false")) multiplexer_1 (
    .in0({32{1'b0}}), .in1(multiplexer_5_out), .out(multiplexer_1_out), .sel(Start));
  Register #(.width(32), .trigger("rising"), .Select("low")) register_1 (
    .D(multiplexer_1_out), .en(1'b1), .Q(register_1_q), .clk(Clock), .clr(Clr), .cs(1'b0), .preset(1'b0));
  Register #(.width(32), .trigger("rising"), .Select("low")) register_2 (
    .D(multiplexer_2_out), .en(1'b1), .Q(bi_prime), .clk(Clock), .clr(Clr), .cs(1'b0), .preset(1'b0));
  Multiplexer #(.select(1), .width(32), .disabled("Z"), .enable("false")) multiplexer_2 (
    .in0(32'h1), .in1(multiplexer_6_out), .out(multiplexer_2_out), .sel(Start));
  Multiplexer #(.select(1), .width(32), .disabled("Z"), .enable("false")) multiplexer_3 (
    .in0(32'h1), .in1(multiplexer_7_out), .out(multiplexer_3_out), .sel(Start));
  Register #(.width(32), .trigger("rising"), .Select("low")) register_3 (
    .D(multiplexer_3_out), .en(1'b1), .Q(register_3_q), .clk(Clock), .clr(Clr), .cs(1'b0), .preset(1'b0));
  Multiplexer #(.select(1), .width(32), .disabled("Z"), .enable("false")) multiplexer_4 (
    .in0(32'h1), .in1(multiplexer_8_out), .out(multiplexer_4_out), .sel(Start));
  Register #(.width(32), .trigger("rising"), .Select("low")) register_4 (
    .D(multiplexer_4_out), .en(1'b1), .Q(register_4_q), .clk(Clock), .clr(Clr), .cs(1'b0), .preset(1'b0));
  sqrX sqrx_1 (
    .in_1(register_1_q), .in_2(bi_prime), .in_3(register_3_q), .in_4(register_4_q), .out_5(sqrx_1_out_5),
    .out_6(sqrx_1_out_6), .out_7(sqrx_1_out_7), .out_8(sqrx_1_out_8));
  sqrX_A sqrx_a_1 (
    .in_1(register_1_q), .in_2(bi_prime), .in_3(register_3_q), .in_4(register_4_q), .out_5(sqrx_a_1_out_5),
    .out_6(sqrx_a_1_out_6), .out_7(sqrx_a_1_out_7), .out_8(sqrx_a_1_out_8));
  Multiplexer #(.select(1), .width(32), .disabled("Z"), .enable("false")) multiplexer_5 (
    .in0(sqrx_1_out_5), .in1(sqrx_a_1_out_5), .out(multiplexer_5_out), .sel(ni_1));
  Multiplexer #(.select(1), .width(32), .disabled("Z"), .enable("false")) multiplexer_6 (
    .in0(sqrx_1_out_6), .in1(sqrx_a_1_out_6), .out(multiplexer_6_out), .sel(ni_1));
  Multiplexer #(.select(1), .width(32), .disabled("Z"), .enable("false")) multiplexer_7 (
    .in0(sqrx_1_out_7), .in1(sqrx_a_1_out_7), .out(multiplexer_7_out), .sel(ni_1));
  Multiplexer #(.select(1), .width(32), .disabled("Z"), .enable("false")) multiplexer_8 (
    .in0(sqrx_1_out_8), .in1(sqrx_a_1_out_8), .out(multiplexer_8_out), .sel(ni_1));
endmodule

module \控制器  (
  input  [5:0] n,
  input  Clock,
  input  Clear,
  output ni_1,
  output Clock_2,
  output Start,
  output Clear_2
);

  wire comparator_1_gt, comparator_2_eq, not_1_out, or_1_out;
  wire [2:0] counter_1_q;

  not not_1 (not_1_out, 1'b1);
  Shift_Register #(.width(1), .length(6), .parallel("true"), .trigger("rising")) shift_register_1 (
    .shift(1'b1), .in(not_1_out), .clk(Clock), .out(ni_1), .load(comparator_2_eq), .clr(Clear), .d0(n[0]),
    .d1(n[1]), .d2(n[2]), .d3(n[3]), .d4(n[4]), .d5(n[5]));  // open: q0, q1, q2, q3, q4, q5
  Counter #(.width(3), .max('h7), .ongoal("wrap"), .trigger("rising"), .behavior("new")) counter_1 (
    .load(1'b0), .count(comparator_1_gt), .Q(counter_1_q), .clk(Clock), .clr(Clear), .preset(1'b0),
    .down(1'b0));  // open: D, carry
  Comparator #(.width(3), .mode("unsigned")) comparator_1 (
    .a(3'b111), .b(counter_1_q), .gt(comparator_1_gt));  // open: eq, lt
  Comparator #(.width(3), .mode("unsigned")) comparator_2 (
    .a(counter_1_q), .b(3'b000), .eq(comparator_2_eq));  // open: gt, lt
  and and_1 (Clock_2, Clock, comparator_1_gt);
  or or_1 (or_1_out, ni_1, Start);
  D_Flip_Flop #(.trigger("rising"), .Pre_Clr_Positions("LEGACY"), .NegatePresetClear("false"), .enable("false"), .NewFFLayout("true")) d_ff_1 (
    .clk(Clock_2), .D(or_1_out), .Q(Start), .reset(Clear));  // open: Qn, preset

  assign Clear_2 = Clear;
endmodule
