// Logisim project 实验4-CS200X-0618-Yuigahama.circ as structural Verilog: 4 circuits, main circuit 四位除法器
module \四位除法器  (
  input  [3:0] n2_3_0,
  input  [3:0] d_3_0,
  output [3:0] quot_3_0,
  output [3:0] rem_3_0
);

  wire comparator_1_eq, comparator_1_gt, comparator_2_eq, comparator_2_gt, comparator_3_eq, comparator_3_gt,
       comparator_4_eq, comparator_4_gt, or_1_out, or_2_out, or_3_out, or_4_out;
  wire [7:0] adder_1_out, adder_2_out, adder_3_out, adder_4_out, bit_extender_1_out, bit_extender_2_out,
       multiplexer_1_out, multiplexer_2_out, multiplexer_3_out, shifter_1_out, shifter_2_out, shifter_3_out,
       shifter_4_out, shifter_5_out, subtractor_1_out, subtractor_2_out, subtractor_3_out, subtractor_4_out;

  assign bit_extender_1_out = {{4{1'b0}}, d_3_0};  // Bit_Extender bit_extender_1
  Shifter #(.width(8), .shift("ll")) shifter_1 (.in(bit_extender_1_out), .\dist (3'b100), .out(shifter_1_out));
  assign bit_extender_2_out = {{4{1'b0}}, n2_3_0};  // Bit_Extender bit_extender_2
  Shifter #(.width(8), .shift("ll")) shifter_2 (.in(bit_extender_2_out), .\dist (3'b001), .out(shifter_2_out));
  Subtractor #(.width(8)) subtractor_1 (
    .a(shifter_2_out), .b(shifter_1_out), .out(subtractor_1_out));  // open: bin, bout
  Adder #(.width(8)) adder_1 (.a(subtractor_1_out), .b(8'h1), .out(adder_1_out));  // open: cin, cout
  Comparator #(.width(4), .mode("unsigned")) comparator_1 (
    .a(shifter_2_out[7:4]), .b(d_3_0), .gt(comparator_1_gt), .eq(comparator_1_eq));  // open: lt
  Multiplexer #(.select(1), .width(8), .disabled("Z"), .enable("false")) multiplexer_1 (
    .in0(shifter_2_out), .in1(adder_1_out), .out(multiplexer_1_out), .sel(or_1_out));
  or or_1 (or_1_out, comparator_1_gt, comparator_1_eq);
  Shifter #(.width(8), .shift("ll")) shifter_3 (.in(multiplexer_1_out), .\dist (3'b001), .out(shifter_3_out));
  Subtractor #(.width(8)) subtractor_2 (
    .a(shifter_3_out), .b(shifter_1_out), .out(subtractor_2_out));  // open: bin, bout
  Adder #(.width(8)) adder_2 (.a(subtractor_2_out), .b(8'h1), .out(adder_2_out));  // open: cin, cout
  Comparator #(.width(4), .mode("unsigned")) comparator_2 (
    .a(shifter_3_out[7:4]), .b(d_3_0), .gt(comparator_2_gt), .eq(comparator_2_eq));  // open: lt
  or or_2 (or_2_out, comparator_2_gt, comparator_2_eq);
  Multiplexer #(.select(1), .width(8), .disabled("Z"), .enable("false")) multiplexer_2 (
    .in0(shifter_3_out), .in1(adder_2_out), .out(multiplexer_2_out), .sel(or_2_out));
  Shifter #(.width(8), .shift("ll")) shifter_4 (.in(multiplexer_2_out), .\dist (3'b001), .out(shifter_4_out));
  Subtractor #(.width(8)) subtractor_3 (
    .a(shifter_4_out), .b(shifter_1_out), .out(subtractor_3_out));  // open: bin, bout
  Comparator #(.width(4), .mode("unsigned")) comparator_3 (
    .a(shifter_4_out[7:4]), .b(d_3_0), .gt(comparator_3_gt), .eq(comparator_3_eq));  // open: lt
  Adder #(.width(8)) adder_3 (.a(subtractor_3_out), .b(8'h1), .out(adder_3_out));  // open: cin, cout
  or or_3 (or_3_out, comparator_3_gt, comparator_3_eq);
  Multiplexer #(.select(1), .width(8), .disabled("Z"), .enable("false")) multiplexer_3 (
    .in0(shifter_4_out), .in1(adder_3_out), .out(multiplexer_3_out), .sel(or_3_out));
  Subtractor #(.width(8)) subtractor_4 (
    .a(shifter_5_out), .b(shifter_1_out), .out(subtractor_4_out));  // open: bin, bout
  Shifter #(.width(8), .shift("ll")) shifter_5 (.in(multiplexer_3_out), .\dist (3'b001), .out(shifter_5_out));
  Adder #(.width(8)) adder_4 (.a(subtractor_4_out), .b(8'h1), .out(adder_4_out));  // open: cin, cout
  Comparator #(.width(4), .mode("unsigned")) comparator_4 (
    .a(shifter_5_out[7:4]), .b(d_3_0), .gt(comparator_4_gt), .eq(comparator_4_eq));  // open: lt
  Multiplexer #(.select(1), .width(8), .disabled("Z"), .enable("false")) multiplexer_4 (
    .in0(shifter_5_out), .in1(adder_4_out), .out({rem_3_0, quot_3_0}), .sel(or_4_out));
  or or_4 (or_4_out, comparator_4_gt, comparator_4_eq);
endmodule

module \四位除法器测试电路  (
  input  [3:0] n2_3_0,
  input  [3:0] d_3_0,
  output [3:0] quot_3_0,
  output [3:0] rem_3_0
);

  \四位除法器  \u_四位除法器_1  (.n2_3_0(n2_3_0), .d_3_0(d_3_0), .quot_3_0(quot_3_0), .rem_3_0(rem_3_0));
endmodule

module \_32位除法器测试电路  (
  input  [31:0] n_31_0,
  input  [31:0] d_31_0,
  output [31:0] quot_31_0,
  output [31:0] rem_31_0
);

  \_32位除法器  \u_32位除法器_1  (.d_31_0(d_31_0), .n2_31_0(n_31_0), .quot_31_0(quot_31_0), .rem_31_0(rem_31_0));
endmodule

module \_32位除法器  (
  input  [31:0] d_31_0,
  input  [31:0] n2_31_0,
  output [31:0] quot_31_0,
  output [31:0] rem_31_0
);

  wire comparator_1_eq, comparator_1_gt, comparator_2_eq, comparator_2_gt, comparator_3_eq, comparator_3_gt,
       comparator_4_eq, comparator_4_gt, comparator_5_eq, comparator_5_gt, comparator_6_eq, comparator_6_gt,
       comparator_7_eq, comparator_7_gt, comparator_8_eq, comparator_8_gt, comparator_9_eq, comparator_9_gt,
       comparator_10_eq, comparator_10_gt, comparator_11_eq, comparator_11_gt, comparator_12_eq,
       comparator_12_gt, comparator_13_eq, comparator_13_gt, comparator_14_eq, comparator_14_gt,
       comparator_15_eq, comparator_15_gt, comparator_16_eq, comparator_16_gt, comparator_17_eq,
       comparator_17_gt, comparator_18_eq, comparator_18_gt, comparator_19_eq, comparator_19_gt,
       comparator_20_eq, comparator_20_gt, comparator_21_eq, comparator_21_gt, comparator_22_eq,
       comparator_22_gt, comparator_23_eq, comparator_23_gt, comparator_24_eq, comparator_24_gt,
       comparator_25_eq, comparator_25_gt, comparator_26_eq, comparator_26_gt, comparator_27_eq,
       comparator_27_gt, comparator_28_eq, comparator_28_gt, comparator_29_eq, comparator_29_gt,
       comparator_30_eq, comparator_30_gt, comparator_31_eq, comparator_31_gt, comparator_32_eq,
       comparator_32_gt;
  wire [31:0] multiplexer_4_out, multiplexer_8_out, multiplexer_15_out, multiplexer_16_out,
       multiplexer_17_out, multiplexer_24_out, multiplexer_28_out, multiplexer_29_out, subtractor_1_out,
       subtractor_2_out, subtractor_3_out, subtractor_4_out, subtractor_5_out, subtractor_6_out,
       subtractor_7_out, subtractor_8_out, subtractor_9_out, subtractor_10_out, subtractor_11_out,
       subtractor_12_out, subtractor_13_out, subtractor_14_out, subtractor_15_out, subtractor_16_out,
       subtractor_17_out, subtractor_18_out, subtractor_19_out, subtractor_20_out, subtractor_21_out,
       subtractor_22_out, subtractor_23_out, subtractor_24_out, subtractor_25_out, subtractor_26_out,
       subtractor_27_out, subtractor_28_out, subtractor_29_out, subtractor_30_out, subtractor_31_out,
       subtractor_32_out;
  wire [31:1] multiplexer_1_out, multiplexer_2_out, multiplexer_3_out, multiplexer_5_out, multiplexer_6_out,
       multiplexer_7_out, multiplexer_9_out, multiplexer_10_out, multiplexer_11_out, multiplexer_12_out,
       multiplexer_13_out, multiplexer_14_out, multiplexer_18_out, multiplexer_19_out, multiplexer_20_out,
       multiplexer_21_out, multiplexer_22_out, multiplexer_23_out, multiplexer_25_out, multiplexer_26_out,
       multiplexer_27_out, multiplexer_30_out, multiplexer_31_out;
  wire [31:31] multiplexer_1_out_2, multiplexer_2_out_2, multiplexer_3_out_2, multiplexer_5_out_2,
       multiplexer_6_out_2, multiplexer_7_out_2, multiplexer_9_out_2, multiplexer_10_out_2,
       multiplexer_11_out_2, multiplexer_12_out_2, multiplexer_13_out_2, multiplexer_14_out_2,
       multiplexer_18_out_2, multiplexer_19_out_2, multiplexer_20_out_2, multiplexer_21_out_2,
       multiplexer_22_out_2, multiplexer_23_out_2, multiplexer_25_out_2, multiplexer_26_out_2,
       multiplexer_27_out_2, multiplexer_30_out_2, multiplexer_31_out_2;

  Subtractor #(.width(32)) subtractor_1 (
    .a({{31{1'b0}}, n2_31_0[31]}), .b(d_31_0), .out(subtractor_1_out));  // open: bin, bout
  Subtractor #(.width(32)) subtractor_2 (
    .a({multiplexer_1_out, n2_31_0[30]}), .b(d_31_0), .out(subtractor_2_out));  // open: bin, bout
  Subtractor #(.width(32)) subtractor_3 (
    .a({multiplexer_2_out, n2_31_0[29]}), .b(d_31_0), .out(subtractor_3_out));  // open: bin, bout
  Subtractor #(.width(32)) subtractor_4 (
    .a({multiplexer_3_out, n2_31_0[28]}), .b(d_31_0), .out(subtractor_4_out));  // open: bin, bout
  Subtractor #(.width(32)) subtractor_5 (
    .a({multiplexer_4_out[30:0], n2_31_0[27]}), .b(d_31_0), .out(subtractor_5_out));  // open: bin, bout
  Subtractor #(.width(32)) subtractor_6 (
    .a({multiplexer_5_out, n2_31_0[26]}), .b(d_31_0), .out(subtractor_6_out));  // open: bin, bout
  Subtractor #(.width(32)) subtractor_7 (
    .a({multiplexer_6_out, n2_31_0[25]}), .b(d_31_0), .out(subtractor_7_out));  // open: bin, bout
  Subtractor #(.width(32)) subtractor_8 (
    .a({multiplexer_7_out, n2_31_0[24]}), .b(d_31_0), .out(subtractor_8_out));  // open: bin, bout
  or or_1 (quot_31_0[31], comparator_1_gt, comparator_1_eq);
  Comparator #(.width(32), .mode("unsigned")) comparator_1 (
    .a({{31{1'b0}}, n2_31_0[31]}), .b(d_31_0), .gt(comparator_1_gt), .eq(comparator_1_eq));  // open: lt
  Comparator #(.width(32), .mode("unsigned")) comparator_2 (
    .a({multiplexer_1_out, n2_31_0[30]}), .b(d_31_0), .gt(comparator_2_gt), .eq(comparator_2_eq));  // open: lt
  or or_2 (quot_31_0[30], comparator_2_gt, comparator_2_eq);
  Comparator #(.width(32), .mode("unsigned")) comparator_3 (
    .a({multiplexer_2_out, n2_31_0[29]}), .b(d_31_0), .gt(comparator_3_gt), .eq(comparator_3_eq));  // open: lt
  or or_3 (quot_31_0[29], comparator_3_gt, comparator_3_eq);
  Comparator #(.width(32), .mode("unsigned")) comparator_4 (
    .a({multiplexer_3_out, n2_31_0[28]}), .b(d_31_0), .gt(comparator_4_gt), .eq(comparator_4_eq));  // open: lt
  or or_4 (quot_31_0[28], comparator_4_gt, comparator_4_eq);
  or or_5 (quot_31_0[27], comparator_5_gt, comparator_5_eq);
  Comparator #(.width(32), .mode("unsigned")) comparator_5 (
    .a({multiplexer_4_out[30:0], n2_31_0[27]}), .b(d_31_0), .gt(comparator_5_gt), .eq(comparator_5_eq));  // open: lt
  or or_6 (quot_31_0[26], comparator_6_gt, comparator_6_eq);
  Comparator #(.width(32), .mode("unsigned")) comparator_6 (
    .a({multiplexer_5_out, n2_31_0[26]}), .b(d_31_0), .gt(comparator_6_gt), .eq(comparator_6_eq));  // open: lt
  or or_7 (quot_31_0[25], comparator_7_gt, comparator_7_eq);
  Comparator #(.width(32), .mode("unsigned")) comparator_7 (
    .a({multiplexer_6_out, n2_31_0[25]}), .b(d_31_0), .gt(comparator_7_gt), .eq(comparator_7_eq));  // open: lt
  or or_8 (quot_31_0[24], comparator_8_gt, comparator_8_eq);
  Comparator #(.width(32), .mode("unsigned")) comparator_8 (
    .a({multiplexer_7_out, n2_31_0[24]}), .b(d_31_0), .gt(comparator_8_gt), .eq(comparator_8_eq));  // open: lt
  Multiplexer #(.select(1), .width(32), .disabled("Z"), .enable("false")) multiplexer_1 (
    .in0({{31{1'b0}}, n2_31_0[31]}), .in1(subtractor_1_out),
    .out({multiplexer_1_out_2[31], multiplexer_1_out}), .sel(quot_31_0[31]));
  Multiplexer #(.select(1), .width(32), .disabled("Z"), .enable("false")) multiplexer_2 (
    .in0({multiplexer_1_out, n2_31_0[30]}), .in1(subtractor_2_out),
    .out({multiplexer_2_out_2[31], multiplexer_2_out}), .sel(quot_31_0[30]));
  Multiplexer #(.select(1), .width(32), .disabled("Z"), .enable("false")) multiplexer_3 (
    .in0({multiplexer_2_out, n2_31_0[29]}), .in1(subtractor_3_out),
    .out({multiplexer_3_out_2[31], multiplexer_3_out}), .sel(quot_31_0[29]));
  Multiplexer #(.select(1), .width(32), .disabled("Z"), .enable("false")) multiplexer_4 (
    .in0({multiplexer_3_out, n2_31_0[28]}), .in1(subtractor_4_out), .out(multiplexer_4_out),
    .sel(quot_31_0[28]));
  Multiplexer #(.select(1), .width(32), .disabled("Z"), .enable("false")) multiplexer_5 (
    .in0({multiplexer_4_out[30:0], n2_31_0[27]}), .in1(subtractor_5_out),
    .out({multiplexer_5_out_2[31], multiplexer_5_out}), .sel(quot_31_0[27]));
  Multiplexer #(.select(1), .width(32), .disabled("Z"), .enable("false")) multiplexer_6 (
    .in0({multiplexer_5_out, n2_31_0[26]}), .in1(subtractor_6_out),
    .out({multiplexer_6_out_2[31], multiplexer_6_out}), .sel(quot_31_0[26]));
  Multiplexer #(.select(1), .width(32), .disabled("Z"), .enable("false")) multiplexer_7 (
    .in0({multiplexer_6_out, n2_31_0[25]}), .in1(subtractor_7_out),
    .out({multiplexer_7_out_2[31], multiplexer_7_out}), .sel(quot_31_0[25]));
  Multiplexer #(.select(1), .width(32), .disabled("Z"), .enable("false")) multiplexer_8 (
    .in0({multiplexer_7_out, n2_31_0[24]}), .in1(subtractor_8_out), .out(multiplexer_8_out),
    .sel(quot_31_0[24]));
  Subtractor #(.width(32)) subtractor_9 (
    .a({multiplexer_8_out[30:0], n2_31_0[23]}), .b(d_31_0), .out(subtractor_9_out));  // open: bin, bout
  Comparator #(.width(32), .mode("unsigned")) comparator_9 (
    .a({multiplexer_8_out[30:0], n2_31_0[23]}), .b(d_31_0), .gt(comparator_9_gt), .eq(comparator_9_eq));  // open: lt
  Subtractor #(.width(32)) subtractor_10 (
    .a({multiplexer_9_out, n2_31_0[22]}), .b(d_31_0), .out(subtractor_10_out));  // open: bin, bout
  Comparator #(.width(32), .mode("unsigned")) comparator_10 (
    .a({multiplexer_9_out, n2_31_0[22]}), .b(d_31_0), .gt(comparator_10_gt), .eq(comparator_10_eq));  // open: lt
  Subtractor #(.width(32)) subtractor_11 (
    .a({multiplexer_10_out, n2_31_0[21]}), .b(d_31_0), .out(subtractor_11_out));  // open: bin, bout
  Comparator #(.width(32), .mode("unsigned")) comparator_11 (
    .a({multiplexer_10_out, n2_31_0[21]}), .b(d_31_0), .gt(comparator_11_gt), .eq(comparator_11_eq));  // open: lt
  Subtractor #(.width(32)) subtractor_12 (
    .a({multiplexer_11_out, n2_31_0[20]}), .b(d_31_0), .out(subtractor_12_out));  // open: bin, bout
  Comparator #(.width(32), .mode("unsigned")) comparator_12 (
    .a({multiplexer_11_out, n2_31_0[20]}), .b(d_31_0), .gt(comparator_12_gt), .eq(comparator_12_eq));  // open: lt
  Subtractor #(.width(32)) subtractor_13 (
    .a({multiplexer_12_out, n2_31_0[19]}), .b(d_31_0), .out(subtractor_13_out));  // open: bin, bout
  Comparator #(.width(32), .mode("unsigned")) comparator_13 (
    .a({multiplexer_12_out, n2_31_0[19]}), .b(d_31_0), .gt(comparator_13_gt), .eq(comparator_13_eq));  // open: lt
  Subtractor #(.width(32)) subtractor_14 (
    .a({multiplexer_13_out, n2_31_0[18]}), .b(d_31_0), .out(subtractor_14_out));  // open: bin, bout
  Comparator #(.width(32), .mode("unsigned")) comparator_14 (
    .a({multiplexer_13_out, n2_31_0[18]}), .b(d_31_0), .gt(comparator_14_gt), .eq(comparator_14_eq));  // open: lt
  Subtractor #(.width(32)) subtractor_15 (
    .a({multiplexer_14_out, n2_31_0[17]}), .b(d_31_0), .out(subtractor_15_out));  // open: bin, bout
  Comparator #(.width(32), .mode("unsigned")) comparator_15 (
    .a({multiplexer_14_out, n2_31_0[17]}), .b(d_31_0), .gt(comparator_15_gt), .eq(comparator_15_eq));  // open: lt
  Subtractor #(.width(32)) subtractor_16 (
    .a({multiplexer_15_out[30:0], n2_31_0[16]}), .b(d_31_0), .out(subtractor_16_out));  // open: bin, bout
  Comparator #(.width(32), .mode("unsigned")) comparator_16 (
    .a({multiplexer_15_out[30:0], n2_31_0[16]}), .b(d_31_0), .gt(comparator_16_gt), .eq(comparator_16_eq));  // open: lt
  or or_9 (quot_31_0[23], comparator_9_gt, comparator_9_eq);
  or or_10 (quot_31_0[22], comparator_10_gt, comparator_10_eq);
  or or_11 (quot_31_0[21], comparator_11_gt, comparator_11_eq);
  or or_12 (quot_31_0[20], comparator_12_gt, comparator_12_eq);
  or or_13 (quot_31_0[19], comparator_13_gt, comparator_13_eq);
  or or_14 (quot_31_0[18], comparator_14_gt, comparator_14_eq);
  or or_15 (quot_31_0[17], comparator_15_gt, comparator_15_eq);
  or or_16 (quot_31_0[16], comparator_16_gt, comparator_16_eq);
  Multiplexer #(.select(1), .width(32), .disabled("Z"), .enable("false")) multiplexer_9 (
    .in0({multiplexer_8_out[30:0], n2_31_0[23]}), .in1(subtractor_9_out),
    .out({multiplexer_9_out_2[31], multiplexer_9_out}), .sel(quot_31_0[23]));
  Multiplexer #(.select(1), .width(32), .disabled("Z"), .enable("false")) multiplexer_10 (
    .in0({multiplexer_9_out, n2_31_0[22]}), .in1(subtractor_10_out),
    .out({multiplexer_10_out_2[31], multiplexer_10_out}), .sel(quot_31_0[22]));
  Multiplexer #(.select(1), .width(32), .disabled("Z"), .enable("false")) multiplexer_11 (
    .in0({multiplexer_10_out, n2_31_0[21]}), .in1(subtractor_11_out),
    .out({multiplexer_11_out_2[31], multiplexer_11_out}), .sel(quot_31_0[21]));
  Multiplexer #(.select(1), .width(32), .disabled("Z"), .enable("false")) multiplexer_12 (
    .in0({multiplexer_11_out, n2_31_0[20]}), .in1(subtractor_12_out),
    .out({multiplexer_12_out_2[31], multiplexer_12_out}), .sel(quot_31_0[20]));
  Multiplexer #(.select(1), .width(32), .disabled("Z"), .enable("false")) multiplexer_13 (
    .in0({multiplexer_12_out, n2_31_0[19]}), .in1(subtractor_13_out),
    .out({multiplexer_13_out_2[31], multiplexer_13_out}), .sel(quot_31_0[19]));
  Multiplexer #(.select(1), .width(32), .disabled("Z"), .enable("false")) multiplexer_14 (
    .in0({multiplexer_13_out, n2_31_0[18]}), .in1(subtractor_14_out),
    .out({multiplexer_14_out_2[31], multiplexer_14_out}), .sel(quot_31_0[18]));
  Multiplexer #(.select(1), .width(32), .disabled("Z"), .enable("false")) multiplexer_15 (
    .in0({multiplexer_14_out, n2_31_0[17]}), .in1(subtractor_15_out), .out(multiplexer_15_out),
    .sel(quot_31_0[17]));
  Multiplexer #(.select(1), .width(32), .disabled("Z"), .enable("false")) multiplexer_16 (
    .in0({multiplexer_15_out[30:0], n2_31_0[16]}), .in1(subtractor_16_out), .out(multiplexer_16_out),
    .sel(quot_31_0[16]));
  Subtractor #(.width(32)) subtractor_17 (
    .a({multiplexer_16_out[30:0], n2_31_0[15]}), .b(d_31_0), .out(subtractor_17_out));  // open: bin, bout
  Subtractor #(.width(32)) subtractor_18 (
    .a({multiplexer_17_out[30:0], n2_31_0[14]}), .b(d_31_0), .out(subtractor_18_out));  // open: bin, bout
  Subtractor #(.width(32)) subtractor_19 (
    .a({multiplexer_18_out, n2_31_0[13]}), .b(d_31_0), .out(subtractor_19_out));  // open: bin, bout
  Subtractor #(.width(32)) subtractor_20 (
    .a({multiplexer_19_out, n2_31_0[12]}), .b(d_31_0), .out(subtractor_20_out));  // open: bin, bout
  Subtractor #(.width(32)) subtractor_21 (
    .a({multiplexer_20_out, n2_31_0[11]}), .b(d_31_0), .out(subtractor_21_out));  // open: bin, bout
  Subtractor #(.width(32)) subtractor_22 (
    .a({multiplexer_21_out, n2_31_0[10]}), .b(d_31_0), .out(subtractor_22_out));  // open: bin, bout
  Subtractor #(.width(32)) subtractor_23 (
    .a({multiplexer_22_out, n2_31_0[9]}), .b(d_31_0), .out(subtractor_23_out));  // open: bin, bout
  Subtractor #(.width(32)) subtractor_24 (
    .a({multiplexer_23_out, n2_31_0[8]}), .b(d_31_0), .out(subtractor_24_out));  // open: bin, bout
  or or_17 (quot_31_0[15], comparator_17_gt, comparator_17_eq);
  Comparator #(.width(32), .mode("unsigned")) comparator_17 (
    .a({multiplexer_16_out[30:0], n2_31_0[15]}), .b(d_31_0), .gt(comparator_17_gt), .eq(comparator_17_eq));  // open: lt
  Comparator #(.width(32), .mode("unsigned")) comparator_18 (
    .a({multiplexer_17_out[30:0], n2_31_0[14]}), .b(d_31_0), .gt(comparator_18_gt), .eq(comparator_18_eq));  // open: lt
  or or_18 (quot_31_0[14], comparator_18_gt, comparator_18_eq);
  Comparator #(.width(32), .mode("unsigned")) comparator_19 (
    .a({multiplexer_18_out, n2_31_0[13]}), .b(d_31_0), .gt(comparator_19_gt), .eq(comparator_19_eq));  // open: lt
  or or_19 (quot_31_0[13], comparator_19_gt, comparator_19_eq);
  Comparator #(.width(32), .mode("unsigned")) comparator_20 (
    .a({multiplexer_19_out, n2_31_0[12]}), .b(d_31_0), .gt(comparator_20_gt), .eq(comparator_20_eq));  // open: lt
  or or_20 (quot_31_0[12], comparator_20_gt, comparator_20_eq);
  Comparator #(.width(32), .mode("unsigned")) comparator_21 (
    .a({multiplexer_20_out, n2_31_0[11]}), .b(d_31_0), .gt(comparator_21_gt), .eq(comparator_21_eq));  // open: lt
  or or_21 (quot_31_0[11], comparator_21_gt, comparator_21_eq);
  Comparator #(.width(32), .mode("unsigned")) comparator_22 (
    .a({multiplexer_21_out, n2_31_0[10]}), .b(d_31_0), .gt(comparator_22_gt), .eq(comparator_22_eq));  // open: lt
  or or_22 (quot_31_0[10], comparator_22_gt, comparator_22_eq);
  or or_23 (quot_31_0[9], comparator_23_gt, comparator_23_eq);
  Comparator #(.width(32), .mode("unsigned")) comparator_23 (
    .a({multiplexer_22_out, n2_31_0[9]}), .b(d_31_0), .gt(comparator_23_gt), .eq(comparator_23_eq));  // open: lt
  or or_24 (quot_31_0[8], comparator_24_gt, comparator_24_eq);
  Comparator #(.width(32), .mode("unsigned")) comparator_24 (
    .a({multiplexer_23_out, n2_31_0[8]}), .b(d_31_0), .gt(comparator_24_gt), .eq(comparator_24_eq));  // open: lt
  Multiplexer #(.select(1), .width(32), .disabled("Z"), .enable("false")) multiplexer_17 (
    .in0({multiplexer_16_out[30:0], n2_31_0[15]}), .in1(subtractor_17_out), .out(multiplexer_17_out),
    .sel(quot_31_0[15]));
  Multiplexer #(.select(1), .width(32), .disabled("Z"), .enable("false")) multiplexer_18 (
    .in0({multiplexer_17_out[30:0], n2_31_0[14]}), .in1(subtractor_18_out),
    .out({multiplexer_18_out_2[31], multiplexer_18_out}), .sel(quot_31_0[14]));
  Multiplexer #(.select(1), .width(32), .disabled("Z"), .enable("false")) multiplexer_19 (
    .in0({multiplexer_18_out, n2_31_0[13]}), .in1(subtractor_19_out),
    .out({multiplexer_19_out_2[31], multiplexer_19_out}), .sel(quot_31_0[13]));
  Multiplexer #(.select(1), .width(32), .disabled("Z"), .enable("false")) multiplexer_20 (
    .in0({multiplexer_19_out, n2_31_0[12]}), .in1(subtractor_20_out),
    .out({multiplexer_20_out_2[31], multiplexer_20_out}), .sel(quot_31_0[12]));
  Multiplexer #(.select(1), .width(32), .disabled("Z"), .enable("false")) multiplexer_21 (
    .in0({multiplexer_20_out, n2_31_0[11]}), .in1(subtractor_21_out),
    .out({multiplexer_21_out_2[31], multiplexer_21_out}), .sel(quot_31_0[11]));
  Multiplexer #(.select(1), .width(32), .disabled("Z"), .enable("false")) multiplexer_22 (
    .in0({multiplexer_21_out, n2_31_0[10]}), .in1(subtractor_22_out),
    .out({multiplexer_22_out_2[31], multiplexer_22_out}), .sel(quot_31_0[10]));
  Multiplexer #(.select(1), .width(32), .disabled("Z"), .enable("false")) multiplexer_23 (
    .in0({multiplexer_22_out, n2_31_0[9]}), .in1(subtractor_23_out),
    .out({multiplexer_23_out_2[31], multiplexer_23_out}), .sel(quot_31_0[9]));
  Multiplexer #(.select(1), .width(32), .disabled("Z"), .enable("false")) multiplexer_24 (
    .in0({multiplexer_23_out, n2_31_0[8]}), .in1(subtractor_24_out), .out(multiplexer_24_out),
    .sel(quot_31_0[8]));
  Subtractor #(.width(32)) subtractor_25 (
    .a({multiplexer_24_out[30:0], n2_31_0[7]}), .b(d_31_0), .out(subtractor_25_out));  // open: bin, bout
  Comparator #(.width(32), .mode("unsigned")) comparator_25 (
    .a({multiplexer_24_out[30:0], n2_31_0[7]}), .b(d_31_0), .gt(comparator_25_gt), .eq(comparator_25_eq));  // open: lt
  Subtractor #(.width(32)) subtractor_26 (
    .a({multiplexer_25_out, n2_31_0[6]}), .b(d_31_0), .out(subtractor_26_out));  // open: bin, bout
  Comparator #(.width(32), .mode("unsigned")) comparator_26 (
    .a({multiplexer_25_out, n2_31_0[6]}), .b(d_31_0), .gt(comparator_26_gt), .eq(comparator_26_eq));  // open: lt
  Subtractor #(.width(32)) subtractor_27 (
    .a({multiplexer_26_out, n2_31_0[5]}), .b(d_31_0), .out(subtractor_27_out));  // open: bin, bout
  Comparator #(.width(32), .mode("unsigned")) comparator_27 (
    .a({multiplexer_26_out, n2_31_0[5]}), .b(d_31_0), .gt(comparator_27_gt), .eq(comparator_27_eq));  // open: lt
  Subtractor #(.width(32)) subtractor_28 (
    .a({multiplexer_27_out, n2_31_0[4]}), .b(d_31_0), .out(subtractor_28_out));  // open: bin, bout
  Comparator #(.width(32), .mode("unsigned")) comparator_28 (
    .a({multiplexer_27_out, n2_31_0[4]}), .b(d_31_0), .gt(comparator_28_gt), .eq(comparator_28_eq));  // open: lt
  Subtractor #(.width(32)) subtractor_29 (
    .a({multiplexer_28_out[30:0], n2_31_0[3]}), .b(d_31_0), .out(subtractor_29_out));  // open: bin, bout
  Comparator #(.width(32), .mode("unsigned")) comparator_29 (
    .a({multiplexer_28_out[30:0], n2_31_0[3]}), .b(d_31_0), .gt(comparator_29_gt), .eq(comparator_29_eq));  // open: lt
  Subtractor #(.width(32)) subtractor_30 (
    .a({multiplexer_29_out[30:0], n2_31_0[2]}), .b(d_31_0), .out(subtractor_30_out));  // open: bin, bout
  Comparator #(.width(32), .mode("unsigned")) comparator_30 (
    .a({multiplexer_29_out[30:0], n2_31_0[2]}), .b(d_31_0), .gt(comparator_30_gt), .eq(comparator_30_eq));  // open: lt
  Subtractor #(.width(32)) subtractor_31 (
    .a({multiplexer_30_out, n2_31_0[1]}), .b(d_31_0), .out(subtractor_31_out));  // open: bin, bout
  Comparator #(.width(32), .mode("unsigned")) comparator_31 (
    .a({multiplexer_30_out, n2_31_0[1]}), .b(d_31_0), .gt(comparator_31_gt), .eq(comparator_31_eq));  // open: lt
  Subtractor #(.width(32)) subtractor_32 (
    .a({multiplexer_31_out, n2_31_0[0]}), .b(d_31_0), .out(subtractor_32_out));  // open: bin, bout
  Comparator #(.width(32), .mode("unsigned")) comparator_32 (
    .a({multiplexer_31_out, n2_31_0[0]}), .b(d_31_0), .gt(comparator_32_gt), .eq(comparator_32_eq));  // open: lt
  or or_25 (quot_31_0[7], comparator_25_gt, comparator_25_eq);
  or or_26 (quot_31_0[6], comparator_26_gt, comparator_26_eq);
  or or_27 (quot_31_0[5], comparator_27_gt, comparator_27_eq);
  or or_28 (quot_31_0[4], comparator_28_gt, comparator_28_eq);
  or or_29 (quot_31_0[3], comparator_29_gt, comparator_29_eq);
  or or_30 (quot_31_0[2], comparator_30_gt, comparator_30_eq);
  or or_31 (quot_31_0[1], comparator_31_gt, comparator_31_eq);
  or or_32 (quot_31_0[0], comparator_32_gt, comparator_32_eq);
  Multiplexer #(.select(1), .width(32), .disabled("Z"), .enable("false")) multiplexer_25 (
    .in0({multiplexer_24_out[30:0], n2_31_0[7]}), .in1(subtractor_25_out),
    .out({multiplexer_25_out_2[31], multiplexer_25_out}), .sel(quot_31_0[7]));
  Multiplexer #(.select(1), .width(32), .disabled("Z"), .enable("false")) multiplexer_26 (
    .in0({multiplexer_25_out, n2_31_0[6]}), .in1(subtractor_26_out),
    .out({multiplexer_26_out_2[31], multiplexer_26_out}), .sel(quot_31_0[6]));
  Multiplexer #(.select(1), .width(32), .disabled("Z"), .enable("false")) multiplexer_27 (
    .in0({multiplexer_26_out, n2_31_0[5]}), .in1(subtractor_27_out),
    .out({multiplexer_27_out_2[31], multiplexer_27_out}), .sel(quot_31_0[5]));
  Multiplexer #(.select(1), .width(32), .disabled("Z"), .enable("false")) multiplexer_28 (
    .in0({multiplexer_27_out, n2_31_0[4]}), .in1(subtractor_28_out), .out(multiplexer_28_out),
    .sel(quot_31_0[4]));
  Multiplexer #(.select(1), .width(32), .disabled("Z"), .enable("false")) multiplexer_29 (
    .in0({multiplexer_28_out[30:0], n2_31_0[3]}), .in1(subtractor_29_out), .out(multiplexer_29_out),
    .sel(quot_31_0[3]));
  Multiplexer #(.select(1), .width(32), .disabled("Z"), .enable("false")) multiplexer_30 (
    .in0({multiplexer_29_out[30:0], n2_31_0[2]}), .in1(subtractor_30_out),
    .out({multiplexer_30_out_2[31], multiplexer_30_out}), .sel(quot_31_0[2]));
  Multiplexer #(.select(1), .width(32), .disabled("Z"), .enable("false")) multiplexer_31 (
    .in0({multiplexer_30_out, n2_31_0[1]}), .in1(subtractor_31_out),
    .out({multiplexer_31_out_2[31], multiplexer_31_out}), .sel(quot_31_0[1]));
  Multiplexer #(.select(1), .width(32), .disabled("Z"), .enable("false")) multiplexer_32 (
    .in0({multiplexer_31_out, n2_31_0[0]}), .in1(subtractor_32_out), .out(rem_31_0), .sel(quot_31_0[0]));
endmodule
